// Logisim project ALU.circ as structural Verilog: 22 circuits, main circuit alu
// 4bitCL
module _4bitCLA (
  input  cin,
  input  P1,
  input  G1,
  input  P2,
  input  G2,
  input  P3,
  input  G3,
  input  P4,
  input  G4,
  output p_prime,
  output g_prime,
  output c1,
  output c2,
  output c3,
  output c4,
  output c5
);

  wire and_2_out, and_3_out, or_1_out, or_2_out, P1cin_out, P2c2_out, p2g1_out, P3c3_out, P4c4_out;

  and and_1 (p_prime, P4, P3, P2, P1);
  and p2g1 (p2g1_out, G1, P2);
  and P1cin (P1cin_out, cin, P1);
  or or_1 (or_1_out, p2g1_out, G2);
  or u_c2 (c2, P1cin_out, G1);
  and and_2 (and_2_out, or_1_out, or_1_out, P3);
  and P2c2 (P2c2_out, c2, P2);
  or or_2 (or_2_out, and_2_out, G3);
  or u_c3 (c3, P2c2_out, G2);
  and and_3 (and_3_out, or_2_out, P4);
  and P3c3 (P3c3_out, c3, P3);
  or or_3 (g_prime, and_3_out, G4);
  or u_c4 (c4, P3c3_out, G3);
  and P4c4 (P4c4_out, c4, P4);
  or u_c5 (c5, P4c4_out, G4);

  assign c1 = cin;
endmodule

module _4bitSum (
  input  c0,
  input  p1,
  input  c1,
  input  p2,
  input  c2,
  input  p3,
  input  c3,
  input  p4,
  output s1,
  output s2,
  output s3,
  output s4
);

  xor xor_1 (s1, c0, p1);
  xor xor_2 (s2, c1, p2);
  xor xor_3 (s3, c2, p3);
  xor xor_4 (s4, c3, p4);
endmodule

module PG (
  input  x1,
  input  y1,
  input  x2,
  input  y2,
  input  x3,
  input  y3,
  input  x4,
  input  y4,
  output p1,
  output g1,
  output p2,
  output g2,
  output p3,
  output g3,
  output p4,
  output g4
);

  xor xor_1 (p1, x1, y1);
  and and_1 (g1, x1, y1);
  xor xor_2 (p2, x2, y2);
  and and_2 (g2, x2, y2);
  xor xor_3 (p3, x3, y3);
  and and_3 (g3, x3, y3);
  xor xor_4 (p4, x4, y4);
  and and_4 (g4, x4, y4);
endmodule

// 16bitAdd
module _16bitAdder (
  input  Cin,
  input  [15:0] B,
  input  [15:0] A,
  output [15:0] Result,
  output over
);

  wire n4bitadder_1_g_prime, n4bitadder_1_p_prime, n4bitadder_2_g_prime, n4bitadder_2_p_prime,
       n4bitadder_3_g_prime, n4bitadder_3_p_prime, n4bitadder_4_g_prime, n4bitadder_4_p_prime, n4bitcla_1_c2,
       n4bitcla_1_c3, n4bitcla_1_c4;

  _4bitAdder u_4bitadder_1 (
    .a1(A[0]), .b1(B[0]), .a2(A[1]), .b2(B[1]), .a3(A[2]), .b3(B[2]), .a4(A[3]), .b4(B[3]), .c1(Cin),
    .p_prime(n4bitadder_1_p_prime), .g_prime(n4bitadder_1_g_prime), .s1(Result[0]), .s2(Result[1]),
    .s3(Result[2]), .s4(Result[3]));  // open: s5
  _4bitAdder u_4bitadder_2 (
    .a1(A[4]), .b1(B[4]), .a2(A[5]), .b2(B[5]), .a3(A[6]), .b3(B[6]), .a4(A[7]), .b4(B[7]),
    .c1(n4bitcla_1_c2), .p_prime(n4bitadder_2_p_prime), .g_prime(n4bitadder_2_g_prime), .s1(Result[4]),
    .s2(Result[5]), .s3(Result[6]), .s4(Result[7]));  // open: s5
  _4bitAdder u_4bitadder_3 (
    .a1(A[8]), .b1(B[8]), .a2(A[9]), .b2(B[9]), .a3(A[10]), .b3(B[10]), .a4(A[11]), .b4(B[11]),
    .c1(n4bitcla_1_c3), .p_prime(n4bitadder_3_p_prime), .g_prime(n4bitadder_3_g_prime), .s1(Result[8]),
    .s2(Result[9]), .s3(Result[10]), .s4(Result[11]));  // open: s5
  _4bitAdder u_4bitadder_4 (
    .a1(A[12]), .b1(B[12]), .a2(A[13]), .b2(B[13]), .a3(A[14]), .b3(B[14]), .a4(A[15]), .b4(B[15]),
    .c1(n4bitcla_1_c4), .p_prime(n4bitadder_4_p_prime), .g_prime(n4bitadder_4_g_prime), .s1(Result[12]),
    .s2(Result[13]), .s3(Result[14]), .s4(Result[15]));  // open: s5
  _4bitCLA u_4bitcla_1 (
    .cin(Cin), .P1(n4bitadder_1_p_prime), .G1(n4bitadder_1_g_prime), .P2(n4bitadder_2_p_prime),
    .G2(n4bitadder_2_g_prime), .P3(n4bitadder_3_p_prime), .G3(n4bitadder_3_g_prime),
    .P4(n4bitadder_4_p_prime), .G4(n4bitadder_4_g_prime), .c2(n4bitcla_1_c2), .c3(n4bitcla_1_c3),
    .c4(n4bitcla_1_c4), .c5(over));  // open: p_prime, g_prime, c1
endmodule

// 4bitAdd
module _4bitAdder (
  input  c1,
  input  a1,
  input  b1,
  input  a2,
  input  b2,
  input  a3,
  input  b3,
  input  a4,
  input  b4,
  output p_prime,
  output g_prime,
  output s1,
  output s2,
  output s3,
  output s4,
  output s5
);

  wire n4bitcla_1_c1, n4bitcla_1_c2, n4bitcla_1_c3, n4bitcla_1_c4, pg_1_g1, pg_1_g2, pg_1_g3, pg_1_g4,
       pg_1_p1, pg_1_p2, pg_1_p3, pg_1_p4;

  PG pg_1 (
    .x1(a1), .y1(b1), .x2(a2), .y2(b2), .x3(a3), .y3(b3), .x4(a4), .y4(b4), .p1(pg_1_p1), .g1(pg_1_g1),
    .p2(pg_1_p2), .g2(pg_1_g2), .p3(pg_1_p3), .g3(pg_1_g3), .p4(pg_1_p4), .g4(pg_1_g4));
  PG pg_2 (
    .x1(a1), .y1(b1), .x2(a2), .y2(b2), .x3(a3), .y3(b3), .x4(a4), .y4(b4), .p1(pg_1_p1), .g1(pg_1_g1),
    .p2(pg_1_p2), .g2(pg_1_g2), .p3(pg_1_p3), .g3(pg_1_g3), .p4(pg_1_p4), .g4(pg_1_g4));
  _4bitCLA u_4bitcla_1 (
    .cin(c1), .P1(pg_1_p1), .G1(pg_1_g1), .P2(pg_1_p2), .G2(pg_1_g2), .P3(pg_1_p3), .G3(pg_1_g3),
    .P4(pg_1_p4), .G4(pg_1_g4), .p_prime(p_prime), .g_prime(g_prime), .c1(n4bitcla_1_c1), .c2(n4bitcla_1_c2),
    .c3(n4bitcla_1_c3), .c4(n4bitcla_1_c4), .c5(s5));
  _4bitSum u_4bitsum_1 (
    .c0(n4bitcla_1_c1), .p1(pg_1_p1), .c1(n4bitcla_1_c2), .p2(pg_1_p2), .c2(n4bitcla_1_c3), .p3(pg_1_p3),
    .c3(n4bitcla_1_c4), .p4(pg_1_p4), .s1(s1), .s2(s2), .s3(s3), .s4(s4));
endmodule

// add
module _32bitAdder (
  input  [31:0] A,
  input  [31:0] B,
  output [31:0] Result,
  output OverFlow
);

  wire n16bitadder_1_over, n16bitadder_2_over, or_1_out, xnor_1_out, xor_1_out;

  _16bitAdder u_16bitadder_1 (.Cin(1'b0), .B(A[15:0]), .A(B[15:0]), .Result(Result[15:0]), .over(n16bitadder_1_over));
  _16bitAdder u_16bitadder_2 (
    .Cin(n16bitadder_1_over), .B(A[31:16]), .A(B[31:16]), .Result(Result[31:16]), .over(n16bitadder_2_over));
  xnor xnor_1 (xnor_1_out, A[31], B[16]);
  xor xor_1 (xor_1_out, Result[31], A[31]);
  or or_1 (or_1_out, xor_1_out, n16bitadder_2_over);
  and and_1 (OverFlow, or_1_out, xnor_1_out);
endmodule

module _32bitOR (
  input  [31:0] A,
  input  [31:0] B,
  output [31:0] Result
);

  or _23 (Result[23], A[23], B[23]);
  or _22 (Result[22], A[22], B[22]);
  or _21 (Result[21], A[21], B[21]);
  or _20 (Result[20], A[20], B[20]);
  or _19 (Result[19], A[19], B[19]);
  or _18 (Result[18], A[18], B[18]);
  or _17 (Result[17], A[17], B[17]);
  or _16 (Result[16], A[16], B[16]);
  or _14 (Result[14], A[14], B[14]);
  or _15 (Result[15], A[15], B[15]);
  or _12 (Result[12], A[12], B[12]);
  or _13 (Result[13], A[13], B[13]);
  or _11 (Result[11], A[11], B[11]);
  or _24 (Result[24], A[31], B[24]);
  or _9 (Result[9], A[9], B[9]);
  or _10 (Result[10], A[10], B[10]);
  or _25 (Result[25], A[30], B[25]);
  or _26 (Result[26], A[29], B[26]);
  or _8 (Result[8], A[8], B[8]);
  or _27 (Result[27], A[28], B[27]);
  or _28 (Result[28], A[27], B[28]);
  or _6 (Result[6], A[6], B[6]);
  or _7 (Result[7], A[7], B[7]);
  or _29 (Result[29], A[26], B[29]);
  or _5 (Result[5], A[5], B[5]);
  or _30 (Result[30], A[25], B[30]);
  or _31 (Result[31], A[24], B[31]);
  or _3 (Result[3], A[3], B[3]);
  or _4 (Result[4], A[4], B[4]);
  or _1 (Result[1], A[1], B[1]);
  or _2 (Result[2], A[2], B[2]);
  or _0 (Result[0], A[0], B[0]);
endmodule

module _32bitAND (
  input  [31:0] A,
  input  [31:0] B,
  output [31:0] Result
);

  and and_1 (Result[23], A[23], B[23]);
  and and_2 (Result[22], A[22], B[22]);
  and and_3 (Result[21], A[21], B[21]);
  and and_4 (Result[20], A[20], B[20]);
  and and_5 (Result[19], A[19], B[19]);
  and and_6 (Result[18], A[18], B[18]);
  and and_7 (Result[17], A[17], B[17]);
  and and_8 (Result[16], A[16], B[16]);
  and and_9 (Result[14], A[14], B[14]);
  and and_10 (Result[15], A[15], B[15]);
  and and_11 (Result[12], A[12], B[12]);
  and and_12 (Result[13], A[13], B[13]);
  and and_13 (Result[11], A[11], B[11]);
  and and_14 (Result[24], A[31], B[24]);
  and and_15 (Result[9], A[9], B[9]);
  and and_16 (Result[10], A[10], B[10]);
  and and_17 (Result[25], A[30], B[25]);
  and and_18 (Result[26], A[29], B[26]);
  and and_19 (Result[8], A[8], B[8]);
  and and_20 (Result[27], A[28], B[27]);
  and and_21 (Result[28], A[27], B[28]);
  and and_22 (Result[6], A[6], B[6]);
  and and_23 (Result[7], A[7], B[7]);
  and and_24 (Result[29], A[26], B[29]);
  and and_25 (Result[5], A[5], B[5]);
  and and_26 (Result[30], A[25], B[30]);
  and and_27 (Result[31], A[24], B[31]);
  and and_28 (Result[3], A[3], B[3]);
  and and_29 (Result[4], A[4], B[4]);
  and and_30 (Result[1], A[1], B[1]);
  and and_31 (Result[2], A[2], B[2]);
  and and_32 (Result[0], A[0], B[0]);
endmodule

module _32bitXOR (
  input  [31:0] A,
  input  [31:0] B,
  output [31:0] Result
);

  xor xor_1 (Result[23], A[23], B[23]);
  xor xor_2 (Result[22], A[22], B[22]);
  xor xor_3 (Result[21], A[21], B[21]);
  xor xor_4 (Result[20], A[20], B[20]);
  xor xor_5 (Result[19], A[19], B[19]);
  xor xor_6 (Result[18], A[18], B[18]);
  xor xor_7 (Result[17], A[17], B[17]);
  xor xor_8 (Result[16], A[16], B[16]);
  xor xor_9 (Result[14], A[14], B[14]);
  xor xor_10 (Result[15], A[15], B[15]);
  xor xor_11 (Result[12], A[12], B[12]);
  xor xor_12 (Result[13], A[13], B[13]);
  xor xor_13 (Result[11], A[11], B[11]);
  xor xor_14 (Result[24], A[31], B[24]);
  xor xor_15 (Result[9], A[9], B[9]);
  xor xor_16 (Result[10], A[10], B[10]);
  xor xor_17 (Result[25], A[30], B[25]);
  xor xor_18 (Result[26], A[29], B[26]);
  xor xor_19 (Result[8], A[8], B[8]);
  xor xor_20 (Result[27], A[28], B[27]);
  xor xor_21 (Result[28], A[27], B[28]);
  xor xor_22 (Result[6], A[6], B[6]);
  xor xor_23 (Result[7], A[7], B[7]);
  xor xor_24 (Result[29], A[26], B[29]);
  xor xor_25 (Result[5], A[5], B[5]);
  xor xor_26 (Result[30], A[25], B[30]);
  xor xor_27 (Result[31], A[24], B[31]);
  xor xor_28 (Result[3], A[3], B[3]);
  xor xor_29 (Result[4], A[4], B[4]);
  xor xor_30 (Result[1], A[1], B[1]);
  xor xor_31 (Result[2], A[2], B[2]);
  xor xor_32 (Result[0], A[0], B[0]);
endmodule

module Mult (
  input  [31:0] A,
  input  [31:0] B,
  output [31:0] Result
);

  Multiplier #(.width(32)) multiplier_1 (.a(A), .b(B), .out(Result));  // open: cin, cout
endmodule

module Mulhu (
  input  [31:0] A,
  input  [31:0] B,
  output [31:0] Result
);

  wire [31:0] bit_extender_1_out, bit_extender_2_out, bit_extender_3_out, bit_extender_4_out,
       bit_extender_5_out, bit_extender_6_out, bit_extender_7_out, bit_extender_8_out, multiplier_1_out,
       multiplier_2_out, multiplier_3_out, n32bitadder_1_result;

  assign bit_extender_1_out = {{16{1'b0}}, A[15:0]};  // Bit_Extender bit_extender_1
  assign bit_extender_2_out = {{16{1'b0}}, B[31:16]};  // Bit_Extender bit_extender_2
  assign bit_extender_3_out = {{16{1'b0}}, B[15:0]};  // Bit_Extender bit_extender_3
  assign bit_extender_4_out = {{16{1'b0}}, A[31:16]};  // Bit_Extender bit_extender_4
  assign bit_extender_5_out = {{16{1'b0}}, B[31:16]};  // Bit_Extender bit_extender_5
  assign bit_extender_6_out = {{16{1'b0}}, A[31:16]};  // Bit_Extender bit_extender_6
  Multiplier #(.width(32)) multiplier_1 (
    .a(bit_extender_1_out), .b(bit_extender_2_out), .out(multiplier_1_out));  // open: cin, cout
  Multiplier #(.width(32)) multiplier_2 (
    .a(bit_extender_3_out), .b(bit_extender_4_out), .out(multiplier_2_out));  // open: cin, cout
  Multiplier #(.width(32)) multiplier_3 (
    .a(bit_extender_5_out), .b(bit_extender_6_out), .out(multiplier_3_out));  // open: cin, cout
  assign bit_extender_7_out = {{16{1'b0}}, multiplier_1_out[31:16]};  // Bit_Extender bit_extender_7
  assign bit_extender_8_out = {{16{1'b0}}, multiplier_2_out[31:16]};  // Bit_Extender bit_extender_8
  _32bitAdder u_32bitadder_1 (
    .B(bit_extender_8_out), .Result(n32bitadder_1_result), .A(bit_extender_7_out));  // open: OverFlow
  _32bitAdder u_32bitadder_2 (.B(multiplier_3_out), .Result(Result), .A(n32bitadder_1_result));  // open: OverFlow
endmodule

module Shifter_Left (
  input  [31:0] A,
  input  [31:0] B,
  output [31:0] Result
);

  Shifter #(.width(32)) shifter_1 (.in(A), .\dist (B[4:0]), .out(Result));
endmodule

module Shifter_Right (
  input  [31:0] A,
  input  [31:0] B,
  output [31:0] Result
);

  Shifter #(.width(32), .shift("lr")) shifter_1 (.in(A), .\dist (B[4:0]), .out(Result));
endmodule

module signed_sra (
  input  [31:0] A,
  input  [31:0] B,
  output [31:0] Result
);

  Shifter #(.width(32), .shift("ar")) shifter_1 (.in(A), .\dist (B[4:0]), .out(Result));
endmodule

module subtract (
  input  [31:0] A,
  input  [31:0] B,
  output [31:0] Result
);

  wire subtractor_1_bout, undriven;

  Subtractor #(.width(32)) subtractor_1 (.a(A), .b(B), .out(Result), .bin(undriven), .bout(subtractor_1_bout));
  Subtractor #(.width(32)) subtractor_2 (.a(A), .b(B), .out(Result), .bin(undriven), .bout(subtractor_1_bout));
endmodule

module compare (
  input  [31:0] A,
  input  [31:0] B,
  output [31:0] Result
);

  wire comparator_1_lt;

  Comparator #(.width(32), .mode("unsigned")) comparator_1 (.a(A), .b(B), .lt(comparator_1_lt));  // open: gt, eq
  assign Result = {{31{1'b0}}, comparator_1_lt};  // Bit_Extender bit_extender_1
endmodule

module mulh (
  input  [31:0] A,
  input  [31:0] B,
  output [31:0] Result
);

  Multiplier #(.width(32)) multiplier_1 (.a(A), .b(B), .cout(Result));  // open: out, cin
endmodule

module mux (
  input  A,
  input  B,
  input  S,
  output R
);

  wire and_1_out, and_2_out, not_1_out;

  not not_1 (not_1_out, S);
  and and_1 (and_1_out, A, not_1_out);
  and and_2 (and_2_out, B, S);
  or or_1 (R, and_1_out, and_2_out);
endmodule

module _2dec (
  input  A,
  input  B,
  input  S,
  output R1,
  output R2,
  output R3,
  output R4
);

  wire not_1_out, not_2_out;

  not not_1 (not_1_out, A);
  not not_2 (not_2_out, B);
  and and_1 (R4, B, A, S);
  and and_2 (R3, B, not_1_out, S);
  and and_3 (R2, not_2_out, A, S);
  and and_4 (R1, not_2_out, not_1_out, S);
endmodule

module _3dec (
  input  A,
  input  B,
  input  C,
  input  E,
  output out_5,
  output out_6,
  output out_7,
  output out_8,
  output out_9,
  output out_10,
  output out_11,
  output out_12
);

  wire n2dec_1_r1, n2dec_1_r2, n2dec_1_r3, n2dec_1_r4, n2dec_2_r1, n2dec_2_r2, n2dec_2_r3, n2dec_2_r4,
       not_1_out;

  _2dec u_2dec_1 (.A(A), .B(B), .S(not_1_out), .R1(n2dec_1_r1), .R2(n2dec_1_r2), .R3(n2dec_1_r3), .R4(n2dec_1_r4));
  not not_1 (not_1_out, C);
  _2dec u_2dec_2 (.A(A), .B(B), .S(C), .R1(n2dec_2_r1), .R2(n2dec_2_r2), .R3(n2dec_2_r3), .R4(n2dec_2_r4));
  and and_1 (out_5, n2dec_1_r1, E);
  and and_2 (out_6, n2dec_1_r2, E);
  and and_3 (out_7, n2dec_1_r3, E);
  and and_4 (out_8, n2dec_1_r4, E);
  and and_5 (out_9, n2dec_2_r1, E);
  and and_6 (out_10, n2dec_2_r2, E);
  and and_7 (out_11, n2dec_2_r3, E);
  and and_8 (out_12, n2dec_2_r4, E);
endmodule

module _4dec (
  input  A,
  input  B,
  input  C,
  input  D,
  output out_5,
  output out_6,
  output out_7,
  output out_8,
  output out_9,
  output out_10,
  output out_11,
  output out_12,
  output out_13,
  output out_14,
  output out_15,
  output out_16,
  output out_17,
  output out_18,
  output out_19,
  output out_20
);

  wire not_1_out;

  not not_1 (not_1_out, D);
  _3dec u_3dec_1 (
    .A(A), .B(B), .C(C), .E(not_1_out), .out_5(out_5), .out_6(out_6), .out_7(out_7), .out_8(out_8),
    .out_9(out_9), .out_10(out_10), .out_11(out_11), .out_12(out_12));
  _3dec u_3dec_2 (
    .A(A), .B(B), .C(C), .E(D), .out_5(out_13), .out_6(out_14), .out_7(out_15), .out_8(out_16),
    .out_9(out_17), .out_10(out_18), .out_11(out_19), .out_12(out_20));
endmodule

module alu (
  input  [31:0] A,
  input  [3:0] ALUSel,
  input  [31:0] B,
  output OverFlow,
  output Zero,
  output [31:0] Result
);

  wire comparator_1_eq, dec_out_5, dec_out_6, dec_out_7, dec_out_9, dec_out_10, dec_out_11, dec_out_12,
       dec_out_13, dec_out_14, dec_out_16, dec_out_17, dec_out_18, dec_out_20;
  wire [31:0] and_result, bit_extender_1_out, bit_extender_2_out, bit_extender_3_out, bit_extender_4_out,
       bit_extender_5_out, bit_extender_6_out, bit_extender_7_out, bit_extender_8_out, bit_extender_9_out,
       bit_extender_10_out, bit_extender_11_out, bit_extender_12_out, bit_extender_13_out, mulh_result,
       mulhu_result, mult_result, n32bitadder_1_result, n32bitand_1_result, n32bitand_2_result,
       n32bitand_3_result, n32bitand_4_result, n32bitand_5_result, n32bitand_6_result, n32bitand_7_result,
       n32bitand_8_result, n32bitand_9_result, n32bitand_10_result, n32bitand_11_result, n32bitand_12_result,
       n32bitand_13_result, n32bitand_14_result, n32bitand_15_result, n32bitand_16_result,
       n32bitand_17_result, n32bitand_18_result, n32bitand_19_result, n32bitand_20_result,
       n32bitand_21_result, n32bitand_22_result, n32bitand_23_result, n32bitand_24_result,
       n32bitand_25_result, n32bitor_1_result, n32bitor_2_result, n32bitor_3_result, n32bitor_4_result,
       n32bitor_5_result, n32bitor_6_result, n32bitor_7_result, n32bitor_8_result, n32bitor_9_result,
       n32bitor_10_result, n32bitor_12_result, or_result, sll_result, slt_result, sra_result, srl_result,
       sub_result, xor_result;

  _4dec dec (
    .A(ALUSel[0]), .B(ALUSel[1]), .C(ALUSel[2]), .D(ALUSel[3]), .out_5(dec_out_5), .out_6(dec_out_6),
    .out_7(dec_out_7), .out_9(dec_out_9), .out_10(dec_out_10), .out_11(dec_out_11), .out_12(dec_out_12),
    .out_13(dec_out_13), .out_14(dec_out_14), .out_16(dec_out_16), .out_17(dec_out_17), .out_18(dec_out_18),
    .out_20(dec_out_20));  // open: out_8, out_15, out_19
  assign bit_extender_1_out = {{31{dec_out_5}}, dec_out_5};  // Bit_Extender bit_extender_1
  assign bit_extender_2_out = {{31{dec_out_6}}, dec_out_6};  // Bit_Extender bit_extender_2
  assign bit_extender_3_out = {{31{dec_out_7}}, dec_out_7};  // Bit_Extender bit_extender_3
  assign bit_extender_4_out = {{31{dec_out_9}}, dec_out_9};  // Bit_Extender bit_extender_4
  assign bit_extender_5_out = {{31{dec_out_10}}, dec_out_10};  // Bit_Extender bit_extender_5
  assign bit_extender_6_out = {{31{dec_out_11}}, dec_out_11};  // Bit_Extender bit_extender_6
  assign bit_extender_7_out = {{31{dec_out_12}}, dec_out_12};  // Bit_Extender bit_extender_7
  assign bit_extender_8_out = {{31{dec_out_13}}, dec_out_13};  // Bit_Extender bit_extender_8
  assign bit_extender_9_out = {{31{dec_out_14}}, dec_out_14};  // Bit_Extender bit_extender_9
  assign bit_extender_10_out = {{31{dec_out_16}}, dec_out_16};  // Bit_Extender bit_extender_10
  assign bit_extender_11_out = {{31{dec_out_17}}, dec_out_17};  // Bit_Extender bit_extender_11
  assign bit_extender_12_out = {{31{dec_out_18}}, dec_out_18};  // Bit_Extender bit_extender_12
  assign bit_extender_13_out = {{31{dec_out_20}}, dec_out_20};  // Bit_Extender bit_extender_13
  _32bitAND u_32bitand_1 (.A(bit_extender_1_out), .B(A), .Result(n32bitand_1_result));
  _32bitAND u_32bitand_2 (.A(bit_extender_1_out), .B(B), .Result(n32bitand_2_result));
  _32bitAND u_32bitand_3 (.A(bit_extender_2_out), .B(A), .Result(n32bitand_3_result));
  _32bitAND u_32bitand_4 (.A(bit_extender_2_out), .B(B), .Result(n32bitand_4_result));
  _32bitAND u_32bitand_5 (.A(bit_extender_3_out), .B(A), .Result(n32bitand_5_result));
  _32bitAND u_32bitand_6 (.A(bit_extender_3_out), .B(B), .Result(n32bitand_6_result));
  _32bitAND u_32bitand_7 (.A(bit_extender_4_out), .B(A), .Result(n32bitand_7_result));
  _32bitAND u_32bitand_8 (.A(bit_extender_4_out), .B(B), .Result(n32bitand_8_result));
  _32bitAND u_32bitand_9 (.A(bit_extender_5_out), .B(A), .Result(n32bitand_9_result));
  _32bitAND u_32bitand_10 (.A(bit_extender_5_out), .B(B), .Result(n32bitand_10_result));
  _32bitAND u_32bitand_11 (.A(bit_extender_6_out), .B(A), .Result(n32bitand_11_result));
  _32bitAND u_32bitand_12 (.A(bit_extender_6_out), .B(B), .Result(n32bitand_12_result));
  _32bitAND u_32bitand_13 (.A(bit_extender_7_out), .B(A), .Result(n32bitand_13_result));
  _32bitAND u_32bitand_14 (.A(bit_extender_7_out), .B(B), .Result(n32bitand_14_result));
  _32bitAND u_32bitand_15 (.A(bit_extender_8_out), .B(A), .Result(n32bitand_15_result));
  _32bitAND u_32bitand_16 (.A(bit_extender_8_out), .B(B), .Result(n32bitand_16_result));
  _32bitAND u_32bitand_17 (.A(bit_extender_9_out), .B(A), .Result(n32bitand_17_result));
  _32bitAND u_32bitand_18 (.A(bit_extender_9_out), .B(B), .Result(n32bitand_18_result));
  _32bitAND u_32bitand_19 (.A(bit_extender_10_out), .B(A), .Result(n32bitand_19_result));
  _32bitAND u_32bitand_20 (.A(bit_extender_10_out), .B(B), .Result(n32bitand_20_result));
  _32bitAND u_32bitand_21 (.A(bit_extender_11_out), .B(A), .Result(n32bitand_21_result));
  _32bitAND u_32bitand_22 (.A(bit_extender_11_out), .B(B), .Result(n32bitand_22_result));
  _32bitAND u_32bitand_23 (.A(bit_extender_12_out), .B(A), .Result(n32bitand_23_result));
  _32bitAND u_32bitand_24 (.A(bit_extender_12_out), .B(B), .Result(n32bitand_24_result));
  _32bitAND u_32bitand_25 (.A(bit_extender_13_out), .B(B), .Result(n32bitand_25_result));
  _32bitAdder u_32bitadder_1 (
    .B(n32bitand_2_result), .Result(n32bitadder_1_result), .OverFlow(OverFlow), .A(n32bitand_1_result));
  Shifter_Left sll (.A(n32bitand_3_result), .B(n32bitand_4_result), .Result(sll_result));
  compare slt (.A(n32bitand_5_result), .B(n32bitand_6_result), .Result(slt_result));
  _32bitXOR \xor  (.A(n32bitand_7_result), .B(n32bitand_8_result), .Result(xor_result));
  Shifter_Right srl (.A(n32bitand_9_result), .B(n32bitand_10_result), .Result(srl_result));
  _32bitOR \or  (.A(n32bitand_11_result), .B(n32bitand_12_result), .Result(or_result));
  _32bitAND \and  (.A(n32bitand_13_result), .B(n32bitand_14_result), .Result(and_result));
  Mult mult (.A(n32bitand_15_result), .B(n32bitand_16_result), .Result(mult_result));
  mulh mulh (.A(n32bitand_17_result), .B(n32bitand_18_result), .Result(mulh_result));
  Mulhu mulhu (.A(n32bitand_19_result), .B(n32bitand_20_result), .Result(mulhu_result));
  subtract sub (.A(n32bitand_21_result), .B(n32bitand_22_result), .Result(sub_result));
  signed_sra sra (.A(n32bitand_23_result), .B(n32bitand_24_result), .Result(sra_result));
  _32bitOR u_32bitor_1 (.A(n32bitadder_1_result), .B(sll_result), .Result(n32bitor_1_result));
  _32bitOR u_32bitor_2 (.A(slt_result), .B(xor_result), .Result(n32bitor_2_result));
  _32bitOR u_32bitor_3 (.A(srl_result), .B(or_result), .Result(n32bitor_3_result));
  _32bitOR u_32bitor_4 (.A(and_result), .B(mult_result), .Result(n32bitor_4_result));
  _32bitOR u_32bitor_5 (.A(mulh_result), .B(mulhu_result), .Result(n32bitor_5_result));
  _32bitOR u_32bitor_6 (.A(sub_result), .B(sra_result), .Result(n32bitor_6_result));
  _32bitOR u_32bitor_7 (.A(n32bitor_1_result), .B(n32bitor_2_result), .Result(n32bitor_7_result));
  _32bitOR u_32bitor_8 (.A(n32bitor_3_result), .B(n32bitor_4_result), .Result(n32bitor_8_result));
  _32bitOR u_32bitor_9 (.A(n32bitor_5_result), .B(n32bitor_6_result), .Result(n32bitor_9_result));
  _32bitOR u_32bitor_10 (.A(n32bitor_7_result), .B(n32bitor_8_result), .Result(n32bitor_10_result));
  _32bitOR u_32bitor_11 (.A(n32bitor_10_result), .B(n32bitor_12_result), .Result(Result));
  _32bitOR u_32bitor_12 (.A(n32bitor_9_result), .B(n32bitand_25_result), .Result(n32bitor_12_result));
  Comparator #(.width(32), .mode("unsigned")) comparator_1 (
    .a({32{1'b0}}), .b(Result), .eq(comparator_1_eq));  // open: gt, lt
  mux mux_1 (.A(1'b0), .B(1'b1), .S(comparator_1_eq), .R(Zero));
endmodule
