// Logisim project alu.circ as structural Verilog: 14 circuits, main circuit main
module add (
  input  [31:0] in_1,
  input  [31:0] in_2,
  output [31:0] Result,
  output Overflow
);

  wire xnor_1_out, xor_1_out;

  Adder #(.width(32)) adder_1 (.a(in_1), .b(in_2), .out(Result), .cin(1'b0));  // open: cout
  xnor xnor_1 (xnor_1_out, in_1[31], in_2[31]);
  xor xor_1 (xor_1_out, Result[31], in_1[31]);
  and and_1 (Overflow, xor_1_out, xnor_1_out);
endmodule

module _32bitOR (
  input  [31:0] A,
  input  [31:0] B,
  output [31:0] Result
);

  assign Result = A | B;  // OR_Gate or_1, 32 bits wide
endmodule

module _32bitAND (
  input  [31:0] A,
  input  [31:0] B,
  output [31:0] Result
);

  assign Result = A & B;  // AND_Gate and_1, 32 bits wide
endmodule

module _32bitXOR (
  input  [31:0] A,
  input  [31:0] B,
  output [31:0] Result
);

  assign Result = A ^ B;  // XOR_Gate xor_1, 32 bits wide
endmodule

module Mult (
  input  [31:0] A,
  input  [31:0] B,
  output [31:0] Result
);

  Multiplier #(.width(32)) multiplier_1 (.a(A), .b(B), .out(Result));  // open: cin, cout
endmodule

module mulh (
  input  [31:0] A,
  input  [31:0] B,
  output [31:0] Result
);

  Multiplier #(.width(32)) multiplier_1 (.a(A), .b(B), .cout(Result));  // open: out, cin
endmodule

module Mulhu (
  input  [31:0] A,
  input  [31:0] B,
  output [31:0] Result
);

  wire [31:0] add_1_result, bit_extender_1_out, bit_extender_2_out, bit_extender_3_out, bit_extender_4_out,
       bit_extender_5_out, bit_extender_6_out, bit_extender_7_out, bit_extender_8_out, multiplier_1_out,
       multiplier_2_out, multiplier_3_out;

  assign bit_extender_1_out = {{16{1'b0}}, A[15:0]};  // Bit_Extender bit_extender_1
  assign bit_extender_2_out = {{16{1'b0}}, B[31:16]};  // Bit_Extender bit_extender_2
  assign bit_extender_3_out = {{16{1'b0}}, B[15:0]};  // Bit_Extender bit_extender_3
  assign bit_extender_4_out = {{16{1'b0}}, A[31:16]};  // Bit_Extender bit_extender_4
  assign bit_extender_5_out = {{16{1'b0}}, B[31:16]};  // Bit_Extender bit_extender_5
  assign bit_extender_6_out = {{16{1'b0}}, A[31:16]};  // Bit_Extender bit_extender_6
  Multiplier #(.width(32)) multiplier_1 (
    .a(bit_extender_1_out), .b(bit_extender_2_out), .out(multiplier_1_out));  // open: cin, cout
  Multiplier #(.width(32)) multiplier_2 (
    .a(bit_extender_3_out), .b(bit_extender_4_out), .out(multiplier_2_out));  // open: cin, cout
  Multiplier #(.width(32)) multiplier_3 (
    .a(bit_extender_5_out), .b(bit_extender_6_out), .out(multiplier_3_out));  // open: cin, cout
  assign bit_extender_7_out = {{16{1'b0}}, multiplier_2_out[31:16]};  // Bit_Extender bit_extender_7
  assign bit_extender_8_out = {{16{1'b0}}, multiplier_1_out[31:16]};  // Bit_Extender bit_extender_8
  add add_1 (.in_1(bit_extender_8_out), .in_2(bit_extender_7_out), .Result(add_1_result));  // open: Overflow
  add add_2 (.in_1(add_1_result), .in_2(multiplier_3_out), .Result(Result));  // open: Overflow
endmodule

module Shifter_Left (
  input  [31:0] A,
  input  [31:0] B,
  output [31:0] Result
);

  Shifter #(.width(32)) shifter_1 (.in(A), .\dist (B[4:0]), .out(Result));
endmodule

module Shifter_Right (
  input  [31:0] A,
  input  [31:0] B,
  output [31:0] Result
);

  Shifter #(.width(32), .shift("lr")) shifter_1 (.in(A), .\dist (B[4:0]), .out(Result));
endmodule

module signed_sra (
  input  [31:0] A,
  input  [31:0] B,
  output [31:0] Result
);

  Shifter #(.width(32), .shift("ar")) shifter_1 (.in(A), .\dist (B[4:0]), .out(Result));
endmodule

module subtract (
  input  [31:0] A,
  input  [31:0] B,
  output [31:0] Result
);

  wire subtractor_1_bout, undriven;

  Subtractor #(.width(32)) subtractor_1 (.a(A), .b(B), .out(Result), .bin(undriven), .bout(subtractor_1_bout));
  Subtractor #(.width(32)) subtractor_2 (.a(A), .b(B), .out(Result), .bin(undriven), .bout(subtractor_1_bout));
endmodule

module compare (
  input  [31:0] A,
  input  [31:0] B,
  output [31:0] Result
);

  wire comparator_1_lt;

  Comparator #(.width(32), .mode("unsigned")) comparator_1 (.a(A), .b(B), .lt(comparator_1_lt));  // open: gt, eq
  assign Result = {{31{1'b0}}, comparator_1_lt};  // Bit_Extender bit_extender_1
endmodule

module alu (
  input  [31:0] A,
  input  [3:0] ALUSel,
  input  [31:0] B,
  output OverFlow,
  output Zero,
  output [31:0] Result
);

  wire comparator_1_eq, decoder_1_out0, decoder_1_out1, decoder_1_out2, decoder_1_out4, decoder_1_out5,
       decoder_1_out6, decoder_1_out7, decoder_1_out8, decoder_1_out9, decoder_1_out11, decoder_1_out12,
       decoder_1_out13, decoder_1_out15;
  wire [31:0] add_result, and_result, bit_extender_1_out, bit_extender_2_out, bit_extender_3_out,
       bit_extender_4_out, bit_extender_5_out, bit_extender_6_out, bit_extender_7_out, bit_extender_8_out,
       bit_extender_9_out, bit_extender_10_out, bit_extender_11_out, bit_extender_12_out,
       bit_extender_13_out, mulh_result, mulhu_result, mult_result, n32bitand_1_result, n32bitand_2_result,
       n32bitand_3_result, n32bitand_4_result, n32bitand_5_result, n32bitand_6_result, n32bitand_7_result,
       n32bitand_8_result, n32bitand_9_result, n32bitand_10_result, n32bitand_11_result, n32bitand_12_result,
       n32bitand_13_result, n32bitand_14_result, n32bitand_15_result, n32bitand_16_result,
       n32bitand_17_result, n32bitand_18_result, n32bitand_19_result, n32bitand_20_result,
       n32bitand_21_result, n32bitand_22_result, n32bitand_23_result, n32bitand_24_result,
       n32bitand_25_result, n32bitor_1_result, n32bitor_2_result, n32bitor_3_result, n32bitor_4_result,
       n32bitor_5_result, n32bitor_6_result, n32bitor_7_result, n32bitor_8_result, n32bitor_9_result,
       n32bitor_10_result, n32bitor_12_result, or_result, sll_result, slt_result, sra_result, srl_result,
       sub_result, xor_result;

  Decoder #(.select(4), .enable("false")) decoder_1 (
    .out0(decoder_1_out0), .out1(decoder_1_out1), .out2(decoder_1_out2), .out4(decoder_1_out4),
    .out5(decoder_1_out5), .out6(decoder_1_out6), .out7(decoder_1_out7), .out8(decoder_1_out8),
    .out9(decoder_1_out9), .out11(decoder_1_out11), .out12(decoder_1_out12), .out13(decoder_1_out13),
    .out15(decoder_1_out15), .sel(ALUSel));  // open: out3, out10, out14
  assign bit_extender_1_out = {{31{decoder_1_out0}}, decoder_1_out0};  // Bit_Extender bit_extender_1
  assign bit_extender_2_out = {{31{decoder_1_out1}}, decoder_1_out1};  // Bit_Extender bit_extender_2
  assign bit_extender_3_out = {{31{decoder_1_out2}}, decoder_1_out2};  // Bit_Extender bit_extender_3
  assign bit_extender_4_out = {{31{decoder_1_out4}}, decoder_1_out4};  // Bit_Extender bit_extender_4
  assign bit_extender_5_out = {{31{decoder_1_out5}}, decoder_1_out5};  // Bit_Extender bit_extender_5
  assign bit_extender_6_out = {{31{decoder_1_out6}}, decoder_1_out6};  // Bit_Extender bit_extender_6
  assign bit_extender_7_out = {{31{decoder_1_out7}}, decoder_1_out7};  // Bit_Extender bit_extender_7
  assign bit_extender_8_out = {{31{decoder_1_out8}}, decoder_1_out8};  // Bit_Extender bit_extender_8
  assign bit_extender_9_out = {{31{decoder_1_out9}}, decoder_1_out9};  // Bit_Extender bit_extender_9
  assign bit_extender_10_out = {{31{decoder_1_out11}}, decoder_1_out11};  // Bit_Extender bit_extender_10
  assign bit_extender_11_out = {{31{decoder_1_out12}}, decoder_1_out12};  // Bit_Extender bit_extender_11
  assign bit_extender_12_out = {{31{decoder_1_out13}}, decoder_1_out13};  // Bit_Extender bit_extender_12
  assign bit_extender_13_out = {{31{decoder_1_out15}}, decoder_1_out15};  // Bit_Extender bit_extender_13
  _32bitAND u_32bitand_1 (.A(bit_extender_1_out), .B(A), .Result(n32bitand_1_result));
  _32bitAND u_32bitand_2 (.A(bit_extender_1_out), .B(B), .Result(n32bitand_2_result));
  _32bitAND u_32bitand_3 (.A(bit_extender_2_out), .B(A), .Result(n32bitand_3_result));
  _32bitAND u_32bitand_4 (.A(bit_extender_2_out), .B(B), .Result(n32bitand_4_result));
  _32bitAND u_32bitand_5 (.A(bit_extender_3_out), .B(A), .Result(n32bitand_5_result));
  _32bitAND u_32bitand_6 (.A(bit_extender_3_out), .B(B), .Result(n32bitand_6_result));
  _32bitAND u_32bitand_7 (.A(bit_extender_4_out), .B(A), .Result(n32bitand_7_result));
  _32bitAND u_32bitand_8 (.A(bit_extender_4_out), .B(B), .Result(n32bitand_8_result));
  _32bitAND u_32bitand_9 (.A(bit_extender_5_out), .B(A), .Result(n32bitand_9_result));
  _32bitAND u_32bitand_10 (.A(bit_extender_5_out), .B(B), .Result(n32bitand_10_result));
  _32bitAND u_32bitand_11 (.A(bit_extender_6_out), .B(A), .Result(n32bitand_11_result));
  _32bitAND u_32bitand_12 (.A(bit_extender_6_out), .B(B), .Result(n32bitand_12_result));
  _32bitAND u_32bitand_13 (.A(bit_extender_7_out), .B(A), .Result(n32bitand_13_result));
  _32bitAND u_32bitand_14 (.A(bit_extender_7_out), .B(B), .Result(n32bitand_14_result));
  _32bitAND u_32bitand_15 (.A(bit_extender_8_out), .B(A), .Result(n32bitand_15_result));
  _32bitAND u_32bitand_16 (.A(bit_extender_8_out), .B(B), .Result(n32bitand_16_result));
  _32bitAND u_32bitand_17 (.A(bit_extender_9_out), .B(A), .Result(n32bitand_17_result));
  _32bitAND u_32bitand_18 (.A(bit_extender_9_out), .B(B), .Result(n32bitand_18_result));
  _32bitAND u_32bitand_19 (.A(bit_extender_10_out), .B(A), .Result(n32bitand_19_result));
  _32bitAND u_32bitand_20 (.A(bit_extender_10_out), .B(B), .Result(n32bitand_20_result));
  _32bitAND u_32bitand_21 (.A(bit_extender_11_out), .B(A), .Result(n32bitand_21_result));
  _32bitAND u_32bitand_22 (.A(bit_extender_11_out), .B(B), .Result(n32bitand_22_result));
  _32bitAND u_32bitand_23 (.A(bit_extender_12_out), .B(A), .Result(n32bitand_23_result));
  _32bitAND u_32bitand_24 (.A(bit_extender_12_out), .B(B), .Result(n32bitand_24_result));
  _32bitAND u_32bitand_25 (.A(bit_extender_13_out), .B(B), .Result(n32bitand_25_result));
  add add (.in_1(n32bitand_1_result), .in_2(n32bitand_2_result), .Result(add_result), .Overflow(OverFlow));
  Shifter_Left sll (.A(n32bitand_3_result), .B(n32bitand_4_result), .Result(sll_result));
  compare slt (.A(n32bitand_5_result), .B(n32bitand_6_result), .Result(slt_result));
  _32bitXOR \xor  (.A(n32bitand_7_result), .B(n32bitand_8_result), .Result(xor_result));
  Shifter_Right srl (.A(n32bitand_9_result), .B(n32bitand_10_result), .Result(srl_result));
  _32bitOR \or  (.A(n32bitand_11_result), .B(n32bitand_12_result), .Result(or_result));
  _32bitAND \and  (.A(n32bitand_13_result), .B(n32bitand_14_result), .Result(and_result));
  Mult mult (.A(n32bitand_15_result), .B(n32bitand_16_result), .Result(mult_result));
  mulh mulh (.A(n32bitand_17_result), .B(n32bitand_18_result), .Result(mulh_result));
  Mulhu mulhu (.A(n32bitand_19_result), .B(n32bitand_20_result), .Result(mulhu_result));
  subtract sub (.A(n32bitand_21_result), .B(n32bitand_22_result), .Result(sub_result));
  signed_sra sra (.A(n32bitand_23_result), .B(n32bitand_24_result), .Result(sra_result));
  _32bitOR u_32bitor_1 (.A(add_result), .B(sll_result), .Result(n32bitor_1_result));
  _32bitOR u_32bitor_2 (.A(slt_result), .B(xor_result), .Result(n32bitor_2_result));
  _32bitOR u_32bitor_3 (.A(srl_result), .B(or_result), .Result(n32bitor_3_result));
  _32bitOR u_32bitor_4 (.A(and_result), .B(mult_result), .Result(n32bitor_4_result));
  _32bitOR u_32bitor_5 (.A(mulh_result), .B(mulhu_result), .Result(n32bitor_5_result));
  _32bitOR u_32bitor_6 (.A(sub_result), .B(sra_result), .Result(n32bitor_6_result));
  _32bitOR u_32bitor_7 (.A(n32bitor_1_result), .B(n32bitor_2_result), .Result(n32bitor_7_result));
  _32bitOR u_32bitor_8 (.A(n32bitor_3_result), .B(n32bitor_4_result), .Result(n32bitor_8_result));
  _32bitOR u_32bitor_9 (.A(n32bitor_5_result), .B(n32bitor_6_result), .Result(n32bitor_9_result));
  _32bitOR u_32bitor_10 (.A(n32bitor_7_result), .B(n32bitor_8_result), .Result(n32bitor_10_result));
  _32bitOR u_32bitor_11 (.A(n32bitor_10_result), .B(n32bitor_12_result), .Result(Result));
  _32bitOR u_32bitor_12 (.A(n32bitor_9_result), .B(n32bitand_25_result), .Result(n32bitor_12_result));
  Comparator #(.width(32), .mode("unsigned")) comparator_1 (
    .a({32{1'b0}}), .b(Result), .eq(comparator_1_eq));  // open: gt, lt
  Multiplexer #(.enable("false")) multiplexer_1 (.in0(1'b0), .in1(1'b1), .out(Zero), .sel(comparator_1_eq));
endmodule

module main (
  input  [31:0] A,
  input  [3:0] ALUSel,
  input  [31:0] B,
  output OverFlow,
  output [31:0] Result,
  output Zero
);

  alu alu (.A(A), .ALUSel(ALUSel), .B(B), .OverFlow(OverFlow), .Result(Result), .Zero(Zero));
endmodule
