// Logisim project 4_bit_adder.circ as structural Verilog: 3 circuits, main circuit Full_Adder
module _4_bit_Adder (
  input  A1,
  input  A2,
  input  A3,
  input  A4,
  input  B1,
  input  B2,
  input  B3,
  input  B4,
  output C1,
  output C2,
  output C3,
  output C4,
  output C5
);

  wire full_adder_1_cout, full_adder_2_cout, half_adder_1_cout;

  Half_Adder half_adder_1 (.A(A1), .B(B1), .S(C1), .Cout(half_adder_1_cout));
  Full_Adder full_adder_1 (.A(A2), .B(B2), .Cin(half_adder_1_cout), .S(C2), .Cout(full_adder_1_cout));
  Full_Adder full_adder_2 (.A(A3), .B(B3), .Cin(full_adder_1_cout), .S(C3), .Cout(full_adder_2_cout));
  Full_Adder full_adder_3 (.A(A4), .B(B4), .Cin(full_adder_2_cout), .S(C4), .Cout(C5));
endmodule

module Full_Adder (
  input  A,
  input  B,
  input  Cin,
  output S,
  output Cout
);

  wire and_1_out, and_2_out, xor_1_out;

  xor xor_1 (xor_1_out, A, B);
  and and_1 (and_1_out, A, B);
  xor xor_2 (S, xor_1_out, Cin);
  and and_2 (and_2_out, xor_1_out, Cin);
  or or_1 (Cout, and_1_out, and_2_out);
endmodule

module Half_Adder (
  input  A,
  input  B,
  output S,
  output Cout
);

  xor xor_1 (S, A, B);
  and and_1 (Cout, A, B);
endmodule
