// Logisim project adder.circ as structural Verilog: 1 circuit, main circuit main
module main (
  input  a0,
  input  b0,
  output s0,
  output c1
);

  xor xor_1 (s0, a0, b0);
  and and_1 (c1, a0, b0);

  // Notes on the sheet:
  //   Adder
endmodule
