// Logisim project alu.circ as structural Verilog: 23 circuits, main circuit alu
// 4bitCL
module L_4bitCLA_f6478cc7 (
  input  cin,
  input  P1,
  input  G1,
  input  P2,
  input  G2,
  input  P3,
  input  G3,
  input  P4,
  input  G4,
  output p_d993ebb1,
  output g_b0806db0,
  output c1,
  output out_13,
  output c3,
  output c4,
  output c5
);

  wire and_2_out, and_3_out, or_1_out, or_2_out, P1cin_out, P2c2_out, p2g1_out, P3c3_out, P4c4_out;

  buf and_1 (p_d993ebb1, P1);  // AND_Gate
  // AND_Gate p2g1 has open pins: out=p2g1_out
  and P1cin (P1cin_out, cin, P1);
  buf or_1 (or_1_out, G2);  // OR_Gate
  or c2 (out_13, P1cin_out, G1);
  and and_2 (and_2_out, or_1_out, P3);
  and P2c2 (P2c2_out, out_13, P2);
  or or_2 (or_2_out, and_2_out, G3);
  or or_3 (c3, P2c2_out, G2);
  and and_3 (and_3_out, or_2_out, P4);
  and P3c3 (P3c3_out, c3, P3);
  or or_4 (g_b0806db0, and_3_out, G4);
  or or_5 (c4, P3c3_out, G3);
  and P4c4 (P4c4_out, c4, P4);
  or or_6 (c5, P4c4_out, G4);

  assign c1 = cin;
endmodule

// 4bitSum
module L_4bitSum_7aad7e6b (
  input  c0,
  input  p1,
  input  c1,
  input  p2,
  input  c2,
  input  p3,
  input  c3,
  input  p4,
  output s1,
  output s2,
  output s3,
  output s4
);

  xor xor_1 (s1, c0, p1);
  xor xor_2 (s2, c1, p2);
  xor xor_3 (s3, c2, p3);
  xor xor_4 (s4, c3, p4);
endmodule

module PG (
  input  x1,
  input  y1,
  input  x2,
  input  y2,
  input  x3,
  input  y3,
  input  x4,
  input  y4,
  output p1,
  output g1,
  output p2,
  output g2,
  output p3,
  output g3,
  output p4,
  output g4
);

  xor xor_1 (p1, x1, y1);
  and and_1 (g1, x1, y1);
  xor xor_2 (p2, x2, y2);
  and and_2 (g2, x2, y2);
  xor xor_3 (p3, x3, y3);
  and and_3 (g3, x3, y3);
  xor xor_4 (p4, x4, y4);
  and and_4 (g4, x4, y4);
endmodule

// 16bitAdd
module L_16bitAdder_6ae20f77 (
  input  Cin,
  input  [15:0] B,
  input  [15:0] A,
  output [15:0] Result,
  output over
);

  wire l_4bitadder_3ee60717_1_g_b0806db0, l_4bitadder_3ee60717_1_p_d993ebb1,
       l_4bitadder_3ee60717_2_g_b0806db0, l_4bitadder_3ee60717_2_p_d993ebb1,
       l_4bitadder_3ee60717_3_g_b0806db0, l_4bitadder_3ee60717_3_p_d993ebb1,
       l_4bitadder_3ee60717_4_g_b0806db0, l_4bitadder_3ee60717_4_p_d993ebb1, l_4bitcla_f6478cc7_1_c3,
       l_4bitcla_f6478cc7_1_c4, l_4bitcla_f6478cc7_1_out_13;

  L_4bitAdder_3ee60717 l_4bitadder_3ee60717_1 (
    .a1(A[0]), .b1(B[0]), .a2(A[1]), .b2(B[1]), .a3(A[2]), .b3(B[2]), .a4(A[3]), .b4(B[3]), .c1(Cin),
    .p_d993ebb1(l_4bitadder_3ee60717_1_p_d993ebb1), .g_b0806db0(l_4bitadder_3ee60717_1_g_b0806db0),
    .s1(Result[0]), .s2(Result[1]), .s3(Result[2]), .s4(Result[3]));  // open: s5
  L_4bitAdder_3ee60717 l_4bitadder_3ee60717_2 (
    .a1(A[4]), .b1(B[4]), .a2(A[5]), .b2(B[5]), .a3(A[6]), .b3(B[6]), .a4(A[7]), .b4(B[7]),
    .c1(l_4bitcla_f6478cc7_1_out_13), .p_d993ebb1(l_4bitadder_3ee60717_2_p_d993ebb1),
    .g_b0806db0(l_4bitadder_3ee60717_2_g_b0806db0), .s1(Result[4]), .s2(Result[5]), .s3(Result[6]),
    .s4(Result[7]));  // open: s5
  L_4bitAdder_3ee60717 l_4bitadder_3ee60717_3 (
    .a1(A[8]), .b1(B[8]), .a2(A[9]), .b2(B[9]), .a3(A[10]), .b3(B[10]), .a4(A[11]), .b4(B[11]),
    .c1(l_4bitcla_f6478cc7_1_c3), .p_d993ebb1(l_4bitadder_3ee60717_3_p_d993ebb1),
    .g_b0806db0(l_4bitadder_3ee60717_3_g_b0806db0), .s1(Result[8]), .s2(Result[9]), .s3(Result[10]),
    .s4(Result[11]));  // open: s5
  L_4bitAdder_3ee60717 l_4bitadder_3ee60717_4 (
    .a1(A[12]), .b1(B[12]), .a2(A[13]), .b2(B[13]), .a3(A[14]), .b3(B[14]), .a4(A[15]), .b4(B[15]),
    .c1(l_4bitcla_f6478cc7_1_c4), .p_d993ebb1(l_4bitadder_3ee60717_4_p_d993ebb1),
    .g_b0806db0(l_4bitadder_3ee60717_4_g_b0806db0), .s1(Result[12]), .s2(Result[13]), .s3(Result[14]),
    .s4(Result[15]));  // open: s5
  L_4bitCLA_f6478cc7 l_4bitcla_f6478cc7_1 (
    .cin(Cin), .P1(l_4bitadder_3ee60717_1_p_d993ebb1), .G1(l_4bitadder_3ee60717_1_g_b0806db0),
    .P2(l_4bitadder_3ee60717_2_p_d993ebb1), .G2(l_4bitadder_3ee60717_2_g_b0806db0),
    .P3(l_4bitadder_3ee60717_3_p_d993ebb1), .G3(l_4bitadder_3ee60717_3_g_b0806db0),
    .P4(l_4bitadder_3ee60717_4_p_d993ebb1), .G4(l_4bitadder_3ee60717_4_g_b0806db0),
    .out_13(l_4bitcla_f6478cc7_1_out_13), .c3(l_4bitcla_f6478cc7_1_c3), .c4(l_4bitcla_f6478cc7_1_c4),
    .c5(over));  // open: p_d993ebb1, g_b0806db0, c1
endmodule

// 4bitAdd
module L_4bitAdder_3ee60717 (
  input  c1,
  input  a1,
  input  b1,
  input  a2,
  input  b2,
  input  a3,
  input  b3,
  input  a4,
  input  b4,
  output p_d993ebb1,
  output g_b0806db0,
  output s1,
  output s2,
  output s3,
  output s4,
  output s5
);

  wire l_4bitcla_f6478cc7_1_c1, l_4bitcla_f6478cc7_1_c3, l_4bitcla_f6478cc7_1_c4,
       l_4bitcla_f6478cc7_1_out_13, pg_1_g1, pg_1_g2, pg_1_g3, pg_1_g4, pg_1_p1, pg_1_p2, pg_1_p3, pg_1_p4;

  PG pg_1 (
    .x1(a1), .y1(b1), .x2(a2), .y2(b2), .x3(a3), .y3(b3), .x4(a4), .y4(b4), .p1(pg_1_p1), .g1(pg_1_g1),
    .p2(pg_1_p2), .g2(pg_1_g2), .p3(pg_1_p3), .g3(pg_1_g3), .p4(pg_1_p4), .g4(pg_1_g4));
  PG pg_2 (
    .p1(pg_1_g1), .g1(pg_1_p2), .p2(pg_1_g2), .g2(pg_1_p3), .p3(pg_1_g3), .g3(pg_1_p4), .p4(pg_1_g4));  // open: x1, y1, x2, y2, x3, y3, x4, y4, g4
  L_4bitCLA_f6478cc7 l_4bitcla_f6478cc7_1 (
    .cin(c1), .P1(pg_1_p1), .G1(pg_1_g1), .P2(pg_1_p2), .G2(pg_1_g2), .P3(pg_1_p3), .G3(pg_1_g3),
    .P4(pg_1_p4), .G4(pg_1_g4), .p_d993ebb1(p_d993ebb1), .g_b0806db0(g_b0806db0),
    .c1(l_4bitcla_f6478cc7_1_c1), .out_13(l_4bitcla_f6478cc7_1_out_13), .c3(l_4bitcla_f6478cc7_1_c3),
    .c4(l_4bitcla_f6478cc7_1_c4), .c5(s5));
  L_4bitSum_7aad7e6b l_4bitsum_7aad7e6b_1 (
    .c0(l_4bitcla_f6478cc7_1_c1), .p1(pg_1_p1), .c1(l_4bitcla_f6478cc7_1_out_13), .p2(pg_1_p2),
    .c2(l_4bitcla_f6478cc7_1_c3), .p3(pg_1_p3), .c3(l_4bitcla_f6478cc7_1_c4), .p4(pg_1_p4), .s1(s1), .s2(s2),
    .s3(s3), .s4(s4));
endmodule

// add
module L_32bitAdder_1c50d512 (
  input  [31:0] A,
  input  [31:0] B,
  output [31:0] Result,
  output OverFlow
);

  wire l_16bitadder_6ae20f77_1_over, l_16bitadder_6ae20f77_2_over, or_1_out, xnor_1_out, xor_1_out;

  L_16bitAdder_6ae20f77 l_16bitadder_6ae20f77_1 (
    .Cin(1'b0), .B(A[15:0]), .A(B[15:0]), .Result(Result[15:0]), .over(l_16bitadder_6ae20f77_1_over));
  L_16bitAdder_6ae20f77 l_16bitadder_6ae20f77_2 (
    .Cin(l_16bitadder_6ae20f77_1_over), .B(A[31:16]), .A(B[31:16]), .Result(Result[31:16]),
    .over(l_16bitadder_6ae20f77_2_over));
  xnor xnor_1 (xnor_1_out, A[31], B[31]);
  xor xor_1 (xor_1_out, Result[31], A[31]);
  or or_1 (or_1_out, xor_1_out, l_16bitadder_6ae20f77_2_over);
  and and_1 (OverFlow, or_1_out, xnor_1_out);
endmodule

module L_32bitOR_f5a0fff7 (
  input  [31:0] A,
  input  [31:0] B,
  output [31:0] Result
);

  assign Result = A | B;  // OR_Gate or_1, 32 bits wide
endmodule

module L_32bitAND_1f608d0c (
  input  [31:0] A,
  input  [31:0] B,
  output [31:0] Result
);

  assign Result = A & B;  // AND_Gate and_1, 32 bits wide
endmodule

module L_32bitXOR_02cf327a (
  input  [31:0] A,
  input  [31:0] B,
  output [31:0] Result
);

  assign Result = A ^ B;  // XOR_Gate xor_1, 32 bits wide
endmodule

module Mult (
  input  [31:0] A,
  input  [31:0] B,
  output [31:0] Result
);

  Multiplier #(.width(32)) multiplier_1 (.a(A), .b(B), .out(Result));  // open: cin, cout
endmodule

module Mulhu (
  input  [31:0] A,
  input  [31:0] B,
  output [31:0] Result
);

  wire [31:0] bit_extender_1_out, bit_extender_2_out, bit_extender_3_out, bit_extender_4_out,
       bit_extender_5_out, bit_extender_6_out, bit_extender_7_out, bit_extender_8_out,
       l_32bitadder_1c50d512_1_result, multiplier_1_out, multiplier_2_out, multiplier_3_out;

  assign bit_extender_1_out = {{16{A[15]}}, A[15:0]};  // Bit_Extender bit_extender_1
  assign bit_extender_2_out = {{16{B[31]}}, B[31:16]};  // Bit_Extender bit_extender_2
  assign bit_extender_3_out = {{16{B[15]}}, B[15:0]};  // Bit_Extender bit_extender_3
  assign bit_extender_4_out = {{16{A[31]}}, A[31:16]};  // Bit_Extender bit_extender_4
  assign bit_extender_5_out = {{16{B[31]}}, B[31:16]};  // Bit_Extender bit_extender_5
  assign bit_extender_6_out = {{16{A[31]}}, A[31:16]};  // Bit_Extender bit_extender_6
  Multiplier #(.width(32)) multiplier_1 (
    .a(bit_extender_1_out), .b(bit_extender_2_out), .out(multiplier_1_out));  // open: cin, cout
  Multiplier #(.width(32)) multiplier_2 (
    .a(bit_extender_3_out), .b(bit_extender_4_out), .out(multiplier_2_out));  // open: cin, cout
  Multiplier #(.width(32)) multiplier_3 (
    .a(bit_extender_5_out), .b(bit_extender_6_out), .out(multiplier_3_out));  // open: cin, cout
  assign bit_extender_7_out = {{16{multiplier_1_out[31]}}, multiplier_1_out[31:16]};  // Bit_Extender bit_extender_7
  assign bit_extender_8_out = {{16{multiplier_2_out[31]}}, multiplier_2_out[31:16]};  // Bit_Extender bit_extender_8
  L_32bitAdder_1c50d512 l_32bitadder_1c50d512_1 (
    .A(bit_extender_7_out), .B(bit_extender_8_out), .Result(l_32bitadder_1c50d512_1_result));  // open: OverFlow
  L_32bitAdder_1c50d512 l_32bitadder_1c50d512_2 (
    .A(l_32bitadder_1c50d512_1_result), .B(multiplier_3_out), .Result(Result));  // open: OverFlow
endmodule

module Shifter_Left_f8a7ce90 (
  input  [31:0] A,
  input  [31:0] B,
  output [31:0] Result
);

  Shifter #(.width(32)) shifter_1 (.in(A), .\dist (B[4:0]), .out(Result));
endmodule

module Shifter_Right_36e8bb3c (
  input  [31:0] A,
  input  [31:0] B,
  output [31:0] Result
);

  Shifter #(.shift("lr"), .width(32)) shifter_1 (.in(A), .\dist (B[4:0]), .out(Result));
endmodule

module signed_sra_d8f4319a (
  input  [31:0] A,
  input  [31:0] B,
  output [31:0] Result
);

  Shifter #(.shift("ar"), .width(32)) shifter_1 (.in(A), .\dist (B[4:0]), .out(Result));
endmodule

module subtract (
  input  [31:0] A,
  input  [31:0] B,
  output [31:0] Result
);

  Subtractor #(.width(32)) subtractor_1 (.a(A), .b(B), .out(Result));  // open: bin, bout
  Subtractor #(.width(32)) subtractor_2 ();  // open: a, b, out, bin, bout
endmodule

module compare (
  input  [31:0] A,
  input  [31:0] B,
  output [31:0] Result
);

  wire comparator_1_lt;

  Comparator #(.mode("unsigned"), .width(32)) comparator_1 (.a(A), .b(B), .lt(comparator_1_lt));  // open: gt, eq
  assign Result = {{31{comparator_1_lt}}, comparator_1_lt};  // Bit_Extender bit_extender_1
endmodule

module mulh (
  input  [31:0] A,
  input  [31:0] B,
  output [31:0] Result
);

  Multiplier #(.width(32)) multiplier_1 (.a(A), .b(B), .cout(Result));  // open: out, cin
endmodule

module mux (
  input  A,
  input  B,
  input  S,
  output R
);

  wire and_1_out, and_2_out, not_1_out;

  not not_1 (not_1_out, S);
  and and_1 (and_1_out, A, not_1_out);
  and and_2 (and_2_out, B, S);
  or or_1 (R, and_1_out, and_2_out);
endmodule

module L_2dec_479c4fda (
  input  A,
  input  B,
  input  S,
  output R1,
  output R2,
  output R3,
  output R4
);

  wire not_1_out, not_2_out;

  not not_1 (not_1_out, A);
  not not_2 (not_2_out, B);
  and and_1 (R4, B, A, S);
  and and_2 (R3, B, not_1_out, S);
  and and_3 (R2, not_2_out, A, S);
  and and_4 (R1, not_2_out, not_1_out, S);
endmodule

module L_3dec_3dd928be (
  input  A,
  input  B,
  input  C,
  input  E,
  output out_5,
  output out_6,
  output out_7,
  output out_8,
  output out_9,
  output out_10,
  output out_11,
  output out_12
);

  wire l_2dec_479c4fda_1_r1, l_2dec_479c4fda_1_r2, l_2dec_479c4fda_1_r3, l_2dec_479c4fda_1_r4,
       l_2dec_479c4fda_2_r1, l_2dec_479c4fda_2_r2, l_2dec_479c4fda_2_r3, l_2dec_479c4fda_2_r4, not_1_out;

  L_2dec_479c4fda l_2dec_479c4fda_1 (
    .A(A), .B(B), .S(not_1_out), .R1(l_2dec_479c4fda_1_r1), .R2(l_2dec_479c4fda_1_r2),
    .R3(l_2dec_479c4fda_1_r3), .R4(l_2dec_479c4fda_1_r4));
  not not_1 (not_1_out, C);
  L_2dec_479c4fda l_2dec_479c4fda_2 (
    .A(A), .B(B), .S(C), .R1(l_2dec_479c4fda_2_r1), .R2(l_2dec_479c4fda_2_r2), .R3(l_2dec_479c4fda_2_r3),
    .R4(l_2dec_479c4fda_2_r4));
  and and_1 (out_5, l_2dec_479c4fda_1_r1, E);
  and and_2 (out_6, l_2dec_479c4fda_1_r2, E);
  and and_3 (out_7, l_2dec_479c4fda_1_r3, E);
  and and_4 (out_8, l_2dec_479c4fda_1_r4, E);
  and and_5 (out_9, l_2dec_479c4fda_2_r1, E);
  and and_6 (out_10, l_2dec_479c4fda_2_r2, E);
  and and_7 (out_11, l_2dec_479c4fda_2_r3, E);
  and and_8 (out_12, l_2dec_479c4fda_2_r4, E);
endmodule

module L_4dec_892604e7 (
  input  A,
  input  B,
  input  C,
  input  D,
  output out_5,
  output out_6,
  output out_7,
  output out_8,
  output out_9,
  output out_10,
  output out_11,
  output out_12,
  output out_13,
  output out_14,
  output out_15,
  output out_16,
  output out_17,
  output out_18,
  output out_19,
  output out_20
);

  wire not_1_out;

  not not_1 (not_1_out, D);
  L_3dec_3dd928be l_3dec_3dd928be_1 (
    .A(A), .B(B), .C(C), .E(not_1_out), .out_5(out_5), .out_6(out_6), .out_7(out_7), .out_8(out_8),
    .out_9(out_9), .out_10(out_10), .out_11(out_11), .out_12(out_12));
  L_3dec_3dd928be l_3dec_3dd928be_2 (
    .A(A), .B(B), .C(C), .E(D), .out_5(out_13), .out_6(out_14), .out_7(out_15), .out_8(out_16),
    .out_9(out_17), .out_10(out_18), .out_11(out_19), .out_12(out_20));
endmodule

module alu (
  input  [31:0] A,
  input  [3:0] ALUSel,
  input  [31:0] B,
  output OverFlow,
  output Zero,
  output [31:0] Result
);

  wire comparator_1_eq, dec_out_5, dec_out_6, dec_out_7, dec_out_9, dec_out_10, dec_out_11, dec_out_12,
       dec_out_13, dec_out_14, dec_out_16, dec_out_17, dec_out_18, dec_out_20;
  wire [31:0] and_result, bit_extender_1_out, bit_extender_2_out, bit_extender_3_out, bit_extender_4_out,
       bit_extender_5_out, bit_extender_6_out, bit_extender_7_out, bit_extender_8_out, bit_extender_9_out,
       bit_extender_10_out, bit_extender_11_out, bit_extender_12_out, bit_extender_13_out,
       l_32bitadder_1c50d512_1_result, l_32bitand_1f608d0c_1_result, l_32bitand_1f608d0c_2_result,
       l_32bitand_1f608d0c_3_result, l_32bitand_1f608d0c_4_result, l_32bitand_1f608d0c_5_result,
       l_32bitand_1f608d0c_6_result, l_32bitand_1f608d0c_7_result, l_32bitand_1f608d0c_8_result,
       l_32bitand_1f608d0c_9_result, l_32bitand_1f608d0c_10_result, l_32bitand_1f608d0c_11_result,
       l_32bitand_1f608d0c_12_result, l_32bitand_1f608d0c_13_result, l_32bitand_1f608d0c_14_result,
       l_32bitand_1f608d0c_15_result, l_32bitand_1f608d0c_16_result, l_32bitand_1f608d0c_17_result,
       l_32bitand_1f608d0c_18_result, l_32bitand_1f608d0c_19_result, l_32bitand_1f608d0c_20_result,
       l_32bitand_1f608d0c_21_result, l_32bitand_1f608d0c_22_result, l_32bitand_1f608d0c_23_result,
       l_32bitand_1f608d0c_24_result, l_32bitand_1f608d0c_25_result, l_32bitor_f5a0fff7_1_result,
       l_32bitor_f5a0fff7_2_result, l_32bitor_f5a0fff7_3_result, l_32bitor_f5a0fff7_4_result,
       l_32bitor_f5a0fff7_5_result, l_32bitor_f5a0fff7_6_result, l_32bitor_f5a0fff7_7_result,
       l_32bitor_f5a0fff7_8_result, l_32bitor_f5a0fff7_9_result, l_32bitor_f5a0fff7_10_result,
       l_32bitor_f5a0fff7_12_result, mulh_1_result, mulhu_1_result, mult_1_result, or_result, sll_result,
       slt_result, sra_result, srl_result, sub_result, xor_result;

  L_4dec_892604e7 dec (
    .A(ALUSel[0]), .B(ALUSel[1]), .C(ALUSel[2]), .D(ALUSel[3]), .out_5(dec_out_5), .out_6(dec_out_6),
    .out_7(dec_out_7), .out_9(dec_out_9), .out_10(dec_out_10), .out_11(dec_out_11), .out_12(dec_out_12),
    .out_13(dec_out_13), .out_14(dec_out_14), .out_16(dec_out_16), .out_17(dec_out_17), .out_18(dec_out_18),
    .out_20(dec_out_20));  // open: out_8, out_15, out_19
  assign bit_extender_1_out = {{31{dec_out_5}}, dec_out_5};  // Bit_Extender bit_extender_1
  assign bit_extender_2_out = {{31{dec_out_6}}, dec_out_6};  // Bit_Extender bit_extender_2
  assign bit_extender_3_out = {{31{dec_out_7}}, dec_out_7};  // Bit_Extender bit_extender_3
  assign bit_extender_4_out = {{31{dec_out_9}}, dec_out_9};  // Bit_Extender bit_extender_4
  assign bit_extender_5_out = {{31{dec_out_10}}, dec_out_10};  // Bit_Extender bit_extender_5
  assign bit_extender_6_out = {{31{dec_out_11}}, dec_out_11};  // Bit_Extender bit_extender_6
  assign bit_extender_7_out = {{31{dec_out_12}}, dec_out_12};  // Bit_Extender bit_extender_7
  assign bit_extender_8_out = {{31{dec_out_13}}, dec_out_13};  // Bit_Extender bit_extender_8
  assign bit_extender_9_out = {{31{dec_out_14}}, dec_out_14};  // Bit_Extender bit_extender_9
  assign bit_extender_10_out = {{31{dec_out_16}}, dec_out_16};  // Bit_Extender bit_extender_10
  assign bit_extender_11_out = {{31{dec_out_17}}, dec_out_17};  // Bit_Extender bit_extender_11
  assign bit_extender_12_out = {{31{dec_out_18}}, dec_out_18};  // Bit_Extender bit_extender_12
  assign bit_extender_13_out = {{31{dec_out_20}}, dec_out_20};  // Bit_Extender bit_extender_13
  L_32bitAND_1f608d0c l_32bitand_1f608d0c_1 (.A(bit_extender_1_out), .B(A), .Result(l_32bitand_1f608d0c_1_result));
  L_32bitAND_1f608d0c l_32bitand_1f608d0c_2 (.A(bit_extender_1_out), .B(B), .Result(l_32bitand_1f608d0c_2_result));
  L_32bitAND_1f608d0c l_32bitand_1f608d0c_3 (.A(bit_extender_2_out), .B(A), .Result(l_32bitand_1f608d0c_3_result));
  L_32bitAND_1f608d0c l_32bitand_1f608d0c_4 (.A(bit_extender_2_out), .B(B), .Result(l_32bitand_1f608d0c_4_result));
  L_32bitAND_1f608d0c l_32bitand_1f608d0c_5 (.A(bit_extender_3_out), .B(A), .Result(l_32bitand_1f608d0c_5_result));
  L_32bitAND_1f608d0c l_32bitand_1f608d0c_6 (.A(bit_extender_3_out), .B(B), .Result(l_32bitand_1f608d0c_6_result));
  L_32bitAND_1f608d0c l_32bitand_1f608d0c_7 (.A(bit_extender_4_out), .B(A), .Result(l_32bitand_1f608d0c_7_result));
  L_32bitAND_1f608d0c l_32bitand_1f608d0c_8 (.A(bit_extender_4_out), .B(B), .Result(l_32bitand_1f608d0c_8_result));
  L_32bitAND_1f608d0c l_32bitand_1f608d0c_9 (.A(bit_extender_5_out), .B(A), .Result(l_32bitand_1f608d0c_9_result));
  L_32bitAND_1f608d0c l_32bitand_1f608d0c_10 (.A(bit_extender_5_out), .B(B), .Result(l_32bitand_1f608d0c_10_result));
  L_32bitAND_1f608d0c l_32bitand_1f608d0c_11 (.A(bit_extender_6_out), .B(A), .Result(l_32bitand_1f608d0c_11_result));
  L_32bitAND_1f608d0c l_32bitand_1f608d0c_12 (.A(bit_extender_6_out), .B(B), .Result(l_32bitand_1f608d0c_12_result));
  L_32bitAND_1f608d0c l_32bitand_1f608d0c_13 (.A(bit_extender_7_out), .B(A), .Result(l_32bitand_1f608d0c_13_result));
  L_32bitAND_1f608d0c l_32bitand_1f608d0c_14 (.A(bit_extender_7_out), .B(B), .Result(l_32bitand_1f608d0c_14_result));
  L_32bitAND_1f608d0c l_32bitand_1f608d0c_15 (.A(bit_extender_8_out), .B(A), .Result(l_32bitand_1f608d0c_15_result));
  L_32bitAND_1f608d0c l_32bitand_1f608d0c_16 (.A(bit_extender_8_out), .B(B), .Result(l_32bitand_1f608d0c_16_result));
  L_32bitAND_1f608d0c l_32bitand_1f608d0c_17 (.A(bit_extender_9_out), .B(A), .Result(l_32bitand_1f608d0c_17_result));
  L_32bitAND_1f608d0c l_32bitand_1f608d0c_18 (.A(bit_extender_9_out), .B(B), .Result(l_32bitand_1f608d0c_18_result));
  L_32bitAND_1f608d0c l_32bitand_1f608d0c_19 (.A(bit_extender_10_out), .B(A), .Result(l_32bitand_1f608d0c_19_result));
  L_32bitAND_1f608d0c l_32bitand_1f608d0c_20 (.A(bit_extender_10_out), .B(B), .Result(l_32bitand_1f608d0c_20_result));
  L_32bitAND_1f608d0c l_32bitand_1f608d0c_21 (.A(bit_extender_11_out), .B(A), .Result(l_32bitand_1f608d0c_21_result));
  L_32bitAND_1f608d0c l_32bitand_1f608d0c_22 (.A(bit_extender_11_out), .B(B), .Result(l_32bitand_1f608d0c_22_result));
  L_32bitAND_1f608d0c l_32bitand_1f608d0c_23 (.A(bit_extender_12_out), .B(A), .Result(l_32bitand_1f608d0c_23_result));
  L_32bitAND_1f608d0c l_32bitand_1f608d0c_24 (.A(bit_extender_12_out), .B(B), .Result(l_32bitand_1f608d0c_24_result));
  L_32bitAND_1f608d0c l_32bitand_1f608d0c_25 (.A(bit_extender_13_out), .B(B), .Result(l_32bitand_1f608d0c_25_result));
  L_32bitAdder_1c50d512 l_32bitadder_1c50d512_1 (
    .A(l_32bitand_1f608d0c_1_result), .B(l_32bitand_1f608d0c_2_result), .OverFlow(OverFlow),
    .Result(l_32bitadder_1c50d512_1_result));
  Shifter_Left_f8a7ce90 sll (.A(l_32bitand_1f608d0c_3_result), .B(l_32bitand_1f608d0c_4_result), .Result(sll_result));
  compare slt (.A(l_32bitand_1f608d0c_5_result), .B(l_32bitand_1f608d0c_6_result), .Result(slt_result));
  L_32bitXOR_02cf327a \xor  (.A(l_32bitand_1f608d0c_7_result), .B(l_32bitand_1f608d0c_8_result), .Result(xor_result));
  Shifter_Right_36e8bb3c srl (.A(l_32bitand_1f608d0c_9_result), .B(l_32bitand_1f608d0c_10_result), .Result(srl_result));
  L_32bitOR_f5a0fff7 \or  (.A(l_32bitand_1f608d0c_11_result), .B(l_32bitand_1f608d0c_12_result), .Result(or_result));
  L_32bitAND_1f608d0c \and  (.A(l_32bitand_1f608d0c_13_result), .B(l_32bitand_1f608d0c_14_result), .Result(and_result));
  Mult mult_1 (.A(l_32bitand_1f608d0c_15_result), .B(l_32bitand_1f608d0c_16_result), .Result(mult_1_result));
  mulh mulh_1 (.A(l_32bitand_1f608d0c_17_result), .B(l_32bitand_1f608d0c_18_result), .Result(mulh_1_result));
  Mulhu mulhu_1 (.A(l_32bitand_1f608d0c_19_result), .B(l_32bitand_1f608d0c_20_result), .Result(mulhu_1_result));
  subtract sub (.A(l_32bitand_1f608d0c_21_result), .B(l_32bitand_1f608d0c_22_result), .Result(sub_result));
  signed_sra_d8f4319a sra (.A(l_32bitand_1f608d0c_23_result), .B(l_32bitand_1f608d0c_24_result), .Result(sra_result));
  L_32bitOR_f5a0fff7 l_32bitor_f5a0fff7_1 (
    .A(l_32bitadder_1c50d512_1_result), .B(sll_result), .Result(l_32bitor_f5a0fff7_1_result));
  L_32bitOR_f5a0fff7 l_32bitor_f5a0fff7_2 (.A(slt_result), .B(xor_result), .Result(l_32bitor_f5a0fff7_2_result));
  L_32bitOR_f5a0fff7 l_32bitor_f5a0fff7_3 (.A(srl_result), .B(or_result), .Result(l_32bitor_f5a0fff7_3_result));
  L_32bitOR_f5a0fff7 l_32bitor_f5a0fff7_4 (.A(and_result), .B(mult_1_result), .Result(l_32bitor_f5a0fff7_4_result));
  L_32bitOR_f5a0fff7 l_32bitor_f5a0fff7_5 (.A(mulh_1_result), .B(mulhu_1_result), .Result(l_32bitor_f5a0fff7_5_result));
  L_32bitOR_f5a0fff7 l_32bitor_f5a0fff7_6 (.A(sub_result), .B(sra_result), .Result(l_32bitor_f5a0fff7_6_result));
  L_32bitOR_f5a0fff7 l_32bitor_f5a0fff7_7 (
    .A(l_32bitor_f5a0fff7_1_result), .B(l_32bitor_f5a0fff7_2_result), .Result(l_32bitor_f5a0fff7_7_result));
  L_32bitOR_f5a0fff7 l_32bitor_f5a0fff7_8 (
    .A(l_32bitor_f5a0fff7_3_result), .B(l_32bitor_f5a0fff7_4_result), .Result(l_32bitor_f5a0fff7_8_result));
  L_32bitOR_f5a0fff7 l_32bitor_f5a0fff7_9 (
    .A(l_32bitor_f5a0fff7_5_result), .B(l_32bitor_f5a0fff7_6_result), .Result(l_32bitor_f5a0fff7_9_result));
  L_32bitOR_f5a0fff7 l_32bitor_f5a0fff7_10 (
    .A(l_32bitor_f5a0fff7_7_result), .B(l_32bitor_f5a0fff7_8_result), .Result(l_32bitor_f5a0fff7_10_result));
  L_32bitOR_f5a0fff7 l_32bitor_f5a0fff7_11 (
    .A(l_32bitor_f5a0fff7_10_result), .B(l_32bitor_f5a0fff7_12_result), .Result(Result));
  L_32bitOR_f5a0fff7 l_32bitor_f5a0fff7_12 (
    .A(l_32bitor_f5a0fff7_9_result), .B(l_32bitand_1f608d0c_25_result), .Result(l_32bitor_f5a0fff7_12_result));
  Comparator #(.mode("unsigned"), .width(32)) comparator_1 (
    .a({32{1'b0}}), .b(Result), .eq(comparator_1_eq));  // open: gt, lt
  mux mux_1 (.A(1'b0), .B(1'b1), .S(comparator_1_eq), .R(Zero));
endmodule

module main (
  input  [31:0] A,
  input  [3:0] ALUSel,
  input  [31:0] B,
  output OverFlow,
  output [31:0] Result,
  output Zero
);

  alu alu_1 (.ALUSel(ALUSel), .A(A), .B(B), .Result(Result), .Zero(Zero), .OverFlow(OverFlow));
endmodule
