// Logisim project processor.circ as structural Verilog: 23 circuits, main circuit processor
// 4bitCLA
module CLA4 (
  input  cin,
  input  P1,
  input  G1,
  input  P2,
  input  G2,
  input  P3,
  input  G3,
  input  P4,
  input  G4,
  output p,
  output g,
  output c1,
  output c2,
  output c3,
  output c4,
  output c5
);

  wire and_2_out, and_3_out, or_1_out, or_3_out, P1cin_out, P2c2_out, p2g1_out, P3c3_out, P4c4_out;

  and p2g1 (p2g1_out, G1, P2);
  or or_1 (or_1_out, p2g1_out, G2);
  and P1cin (P1cin_out, cin, P1);
  and and_1 (p, P1, P2, P3, P4);
  and and_2 (and_2_out, or_1_out, P3);
  or or_2 (c2, P1cin_out, G1);
  or or_3 (or_3_out, and_2_out, G3);
  and P2c2 (P2c2_out, c2, P2);
  and and_3 (and_3_out, or_3_out, P4);
  or or_4 (c3, P2c2_out, G2);
  and P3c3 (P3c3_out, c3, P3);
  or or_5 (g, and_3_out, G4);
  or or_6 (c4, P3c3_out, G3);
  and P4c4 (P4c4_out, c4, P4);
  or or_7 (c5, P4c4_out, G4);

  assign c1 = cin;
endmodule

// 4bitSum
module Sum4 (
  input  c0,
  input  p1,
  input  c1,
  input  p2,
  input  c2,
  input  p3,
  input  c3,
  input  p4,
  output s1,
  output s2,
  output s3,
  output s4
);

  xor xor_1 (s1, c0, p1);
  xor xor_2 (s2, c1, p2);
  xor xor_3 (s3, c2, p3);
  xor xor_4 (s4, c3, p4);
endmodule

module PG (
  input  x1,
  input  y1,
  input  x2,
  input  y2,
  input  x3,
  input  y3,
  input  x4,
  input  y4,
  output p1,
  output g1,
  output p2,
  output g2,
  output p3,
  output g3,
  output p4,
  output g4
);

  xor xor_1 (p1, x1, y1);
  and and_1 (g1, x1, y1);
  xor xor_2 (p2, x2, y2);
  and and_2 (g2, x2, y2);
  xor xor_3 (p3, x3, y3);
  and and_3 (g3, x3, y3);
  xor xor_4 (p4, x4, y4);
  and and_4 (g4, x4, y4);
endmodule

// 4bitAdd
module Adder4 (
  input  c1,
  input  a1,
  input  b1,
  input  a2,
  input  b2,
  input  a3,
  input  b3,
  input  a4,
  input  b4,
  output p_d993ebb1,
  output g_b0806db0,
  output s1,
  output s2,
  output s3,
  output s4,
  output s5
);

  wire cla4_1_c1, cla4_1_c2, cla4_1_c3, cla4_1_c4, pg_1_g1, pg_1_g2, pg_1_g3, pg_1_g4, pg_1_p1, pg_1_p2,
       pg_1_p3, pg_1_p4;

  PG pg_1 (
    .x1(a1), .y1(b1), .x2(a2), .y2(b2), .x3(a3), .y3(b3), .x4(a4), .y4(b4), .p1(pg_1_p1), .g1(pg_1_g1),
    .p2(pg_1_p2), .g2(pg_1_g2), .p3(pg_1_p3), .g3(pg_1_g3), .p4(pg_1_p4), .g4(pg_1_g4));
  CLA4 cla4_1 (
    .cin(c1), .P1(pg_1_p1), .G1(pg_1_g1), .P2(pg_1_p2), .G2(pg_1_g2), .P3(pg_1_p3), .G3(pg_1_g3),
    .P4(pg_1_p4), .G4(pg_1_g4), .p(p_d993ebb1), .g(g_b0806db0), .c1(cla4_1_c1), .c2(cla4_1_c2),
    .c3(cla4_1_c3), .c4(cla4_1_c4), .c5(s5));
  Sum4 sum4_1 (
    .c0(cla4_1_c1), .p1(pg_1_p1), .c1(cla4_1_c2), .p2(pg_1_p2), .c2(cla4_1_c3), .p3(pg_1_p3), .c3(cla4_1_c4),
    .p4(pg_1_p4), .s1(s1), .s2(s2), .s3(s3), .s4(s4));
endmodule

// 16bitAdd
module Adder16 (
  input  Cin,
  input  [15:0] B,
  input  [15:0] A,
  output [15:0] Result,
  output over
);

  wire adder4_1_g_b0806db0, adder4_1_p_d993ebb1, adder4_2_g_b0806db0, adder4_2_p_d993ebb1,
       adder4_3_g_b0806db0, adder4_3_p_d993ebb1, adder4_4_g_b0806db0, adder4_4_p_d993ebb1, cla4_1_c2,
       cla4_1_c3, cla4_1_c4;

  Adder4 adder4_1 (
    .a1(A[0]), .b1(B[0]), .a2(A[1]), .b2(B[1]), .a3(A[2]), .b3(B[2]), .a4(A[3]), .b4(B[3]), .c1(Cin),
    .p_d993ebb1(adder4_1_p_d993ebb1), .g_b0806db0(adder4_1_g_b0806db0), .s1(Result[0]), .s2(Result[1]),
    .s3(Result[2]), .s4(Result[3]));  // open: s5
  Adder4 adder4_2 (
    .a1(A[4]), .b1(B[4]), .a2(A[5]), .b2(B[5]), .a3(A[6]), .b3(B[6]), .a4(A[7]), .b4(B[7]), .c1(cla4_1_c2),
    .p_d993ebb1(adder4_2_p_d993ebb1), .g_b0806db0(adder4_2_g_b0806db0), .s1(Result[4]), .s2(Result[5]),
    .s3(Result[6]), .s4(Result[7]));  // open: s5
  Adder4 adder4_3 (
    .a1(A[8]), .b1(B[8]), .a2(A[9]), .b2(B[9]), .a3(A[10]), .b3(B[10]), .a4(A[11]), .b4(B[11]),
    .c1(cla4_1_c3), .p_d993ebb1(adder4_3_p_d993ebb1), .g_b0806db0(adder4_3_g_b0806db0), .s1(Result[8]),
    .s2(Result[9]), .s3(Result[10]), .s4(Result[11]));  // open: s5
  Adder4 adder4_4 (
    .a1(A[12]), .b1(B[12]), .a2(A[13]), .b2(B[13]), .a3(A[14]), .b3(B[14]), .a4(A[15]), .b4(B[15]),
    .c1(cla4_1_c4), .p_d993ebb1(adder4_4_p_d993ebb1), .g_b0806db0(adder4_4_g_b0806db0), .s1(Result[12]),
    .s2(Result[13]), .s3(Result[14]), .s4(Result[15]));  // open: s5
  CLA4 cla4_1 (
    .cin(Cin), .P1(adder4_1_p_d993ebb1), .G1(adder4_1_g_b0806db0), .P2(adder4_2_p_d993ebb1),
    .G2(adder4_2_g_b0806db0), .P3(adder4_3_p_d993ebb1), .G3(adder4_3_g_b0806db0), .P4(adder4_4_p_d993ebb1),
    .G4(adder4_4_g_b0806db0), .c2(cla4_1_c2), .c3(cla4_1_c3), .c4(cla4_1_c4), .c5(over));  // open: p, g, c1
endmodule

// add
module Adder32 (
  input  [31:0] A,
  input  [31:0] B,
  output [31:0] Result,
  output OverFlow
);

  wire adder16_1_over, adder16_2_over, or_1_out, xnor_1_out, xor_1_out;

  Adder16 adder16_1 (.Cin(1'b0), .B(A[15:0]), .A(B[15:0]), .Result(Result[15:0]), .over(adder16_1_over));
  Adder16 adder16_2 (.Cin(adder16_1_over), .B(A[31:16]), .A(B[31:16]), .Result(Result[31:16]), .over(adder16_2_over));
  xnor xnor_1 (xnor_1_out, A[31], B[31]);
  xor xor_1 (xor_1_out, Result[31], A[31]);
  or or_1 (or_1_out, xor_1_out, adder16_2_over);
  and and_1 (OverFlow, or_1_out, xnor_1_out);
endmodule

// or
module OR32 (
  input  [31:0] A,
  input  [31:0] B,
  output [31:0] Result
);

  assign Result = A | B;  // OR_Gate or_1, 32 bits wide
endmodule

// and
module AND32 (
  input  [31:0] A,
  input  [31:0] B,
  output [31:0] Result
);

  assign Result = A & B;  // AND_Gate and_1, 32 bits wide
endmodule

// xor
module XOR32 (
  input  [31:0] A,
  input  [31:0] B,
  output [31:0] Result
);

  assign Result = A ^ B;  // XOR_Gate xor_1, 32 bits wide
endmodule

// mult
module Mult (
  input  [31:0] A,
  input  [31:0] B,
  output [31:0] Result
);

  Multiplier #(.width(32)) multiplier_1 (.a(A), .b(B), .out(Result));  // open: cin, cout
endmodule

// mulhu
module Mulhu (
  input  [31:0] A,
  input  [31:0] B,
  output [31:0] Result
);

  wire [31:0] adder32_1_result, bit_extender_1_out, bit_extender_2_out, bit_extender_3_out,
       bit_extender_4_out, bit_extender_5_out, bit_extender_6_out, bit_extender_7_out, bit_extender_8_out,
       multiplier_1_out, multiplier_2_out, multiplier_3_out;

  assign bit_extender_1_out = {{16{A[15]}}, A[15:0]};  // Bit_Extender bit_extender_1
  assign bit_extender_2_out = {{16{B[31]}}, B[31:16]};  // Bit_Extender bit_extender_2
  assign bit_extender_3_out = {{16{B[15]}}, B[15:0]};  // Bit_Extender bit_extender_3
  assign bit_extender_4_out = {{16{A[31]}}, A[31:16]};  // Bit_Extender bit_extender_4
  assign bit_extender_5_out = {{16{B[31]}}, B[31:16]};  // Bit_Extender bit_extender_5
  assign bit_extender_6_out = {{16{A[31]}}, A[31:16]};  // Bit_Extender bit_extender_6
  Multiplier #(.width(32)) multiplier_1 (
    .a(bit_extender_1_out), .b(bit_extender_2_out), .out(multiplier_1_out));  // open: cin, cout
  Multiplier #(.width(32)) multiplier_2 (
    .a(bit_extender_3_out), .b(bit_extender_4_out), .out(multiplier_2_out));  // open: cin, cout
  Multiplier #(.width(32)) multiplier_3 (
    .a(bit_extender_5_out), .b(bit_extender_6_out), .out(multiplier_3_out));  // open: cin, cout
  assign bit_extender_7_out = {{16{multiplier_1_out[31]}}, multiplier_1_out[31:16]};  // Bit_Extender bit_extender_7
  assign bit_extender_8_out = {{16{multiplier_2_out[31]}}, multiplier_2_out[31:16]};  // Bit_Extender bit_extender_8
  Adder32 adder32_1 (.A(bit_extender_7_out), .B(bit_extender_8_out), .Result(adder32_1_result));  // open: OverFlow
  Adder32 adder32_2 (.A(adder32_1_result), .B(multiplier_3_out), .Result(Result));  // open: OverFlow
endmodule

// sll
module Shifter_Left (
  input  [31:0] A,
  input  [31:0] B,
  output [31:0] Result
);

  Shifter #(.width(32)) shifter_1 (.in(A), .\dist (B[4:0]), .out(Result));
endmodule

// srl
module Shifter_Right (
  input  [31:0] A,
  input  [31:0] B,
  output [31:0] Result
);

  Shifter #(.shift("lr"), .width(32)) shifter_1 (.in(A), .\dist (B[4:0]), .out(Result));
endmodule

// sra
module signed_sra (
  input  [31:0] A,
  input  [31:0] B,
  output [31:0] Result
);

  Shifter #(.shift("ar"), .width(32)) shifter_1 (.in(A), .\dist (B[4:0]), .out(Result));
endmodule

// sub
module subtract (
  input  [31:0] A,
  input  [31:0] B,
  output [31:0] Result
);

  Subtractor #(.width(32)) subtractor_1 (.a(A), .b(B), .out(Result));  // open: bin, bout
endmodule

// slt
module compare (
  input  [31:0] A,
  input  [31:0] B,
  output [31:0] Result
);

  wire comparator_1_lt;

  Comparator #(.width(32)) comparator_1 (.a(A), .b(B), .lt(comparator_1_lt));  // open: gt, eq
  assign Result = {{31{1'b0}}, comparator_1_lt};  // Bit_Extender bit_extender_1
endmodule

// sltu
module compareu (
  input  [31:0] A,
  input  [31:0] B,
  output [31:0] Result
);

  wire comparator_1_lt;

  Comparator #(.mode("unsigned"), .width(32)) comparator_1 (.a(A), .b(B), .lt(comparator_1_lt));  // open: gt, eq
  assign Result = {{31{comparator_1_lt}}, comparator_1_lt};  // Bit_Extender bit_extender_1
endmodule

module mulh (
  input  [31:0] A,
  input  [31:0] B,
  output [31:0] Result
);

  Multiplier #(.width(32)) multiplier_1 (.a(A), .b(B), .cout(Result));  // open: out, cin
endmodule

// alu
module alucirc (
  input  [31:0] A,
  input  [3:0] ALUSel,
  input  [31:0] B,
  output OverFlow,
  output Zero,
  output [31:0] Result
);

  wire comparator_1_eq, decoder_1_out0, decoder_1_out1, decoder_1_out2, decoder_1_out3, decoder_1_out4,
       decoder_1_out5, decoder_1_out6, decoder_1_out7, decoder_1_out8, decoder_1_out9, decoder_1_out11,
       decoder_1_out12, decoder_1_out13, decoder_1_out15;
  wire [31:0] adder32_1_result, and32_1_result, and32_2_result, and32_3_result, and32_4_result,
       and32_5_result, and32_6_result, and32_7_result, and32_8_result, and32_9_result, and32_10_result,
       and32_11_result, and32_12_result, and32_13_result, and32_14_result, and32_15_result, and32_16_result,
       and32_17_result, and32_18_result, and32_19_result, and32_20_result, and32_21_result, and32_22_result,
       and32_23_result, and32_24_result, and32_25_result, and32_26_result, and32_27_result, and32_28_result,
       bit_extender_1_out, bit_extender_2_out, bit_extender_3_out, bit_extender_4_out, bit_extender_5_out,
       bit_extender_6_out, bit_extender_7_out, bit_extender_8_out, bit_extender_9_out, bit_extender_10_out,
       bit_extender_11_out, bit_extender_12_out, bit_extender_13_out, bit_extender_14_out, compare_1_result,
       compareu_1_result, mulh_1_result, mulhu_1_result, mult_1_result, or32_1_result, or32_2_result,
       or32_3_result, or32_4_result, or32_5_result, or32_6_result, or32_7_result, or32_8_result,
       or32_9_result, or32_10_result, or32_11_result, or32_12_result, or32_14_result, shifter_left_1_result,
       shifter_right_1_result, signed_sra_1_result, subtract_1_result, xor32_1_result;

  Decoder #(.enable("false"), .select(4)) decoder_1 (
    .out0(decoder_1_out0), .out1(decoder_1_out1), .out2(decoder_1_out2), .out3(decoder_1_out3),
    .out4(decoder_1_out4), .out5(decoder_1_out5), .out6(decoder_1_out6), .out7(decoder_1_out7),
    .out8(decoder_1_out8), .out9(decoder_1_out9), .out11(decoder_1_out11), .out12(decoder_1_out12),
    .out13(decoder_1_out13), .out15(decoder_1_out15), .sel(ALUSel));  // open: out10, out14
  assign bit_extender_1_out = {{31{decoder_1_out0}}, decoder_1_out0};  // Bit_Extender bit_extender_1
  assign bit_extender_2_out = {{31{decoder_1_out1}}, decoder_1_out1};  // Bit_Extender bit_extender_2
  assign bit_extender_3_out = {{31{decoder_1_out2}}, decoder_1_out2};  // Bit_Extender bit_extender_3
  assign bit_extender_4_out = {{31{decoder_1_out4}}, decoder_1_out4};  // Bit_Extender bit_extender_4
  assign bit_extender_5_out = {{31{decoder_1_out5}}, decoder_1_out5};  // Bit_Extender bit_extender_5
  assign bit_extender_6_out = {{31{decoder_1_out6}}, decoder_1_out6};  // Bit_Extender bit_extender_6
  assign bit_extender_7_out = {{31{decoder_1_out7}}, decoder_1_out7};  // Bit_Extender bit_extender_7
  assign bit_extender_8_out = {{31{decoder_1_out8}}, decoder_1_out8};  // Bit_Extender bit_extender_8
  assign bit_extender_9_out = {{31{decoder_1_out9}}, decoder_1_out9};  // Bit_Extender bit_extender_9
  assign bit_extender_10_out = {{31{decoder_1_out11}}, decoder_1_out11};  // Bit_Extender bit_extender_10
  assign bit_extender_11_out = {{31{decoder_1_out12}}, decoder_1_out12};  // Bit_Extender bit_extender_11
  assign bit_extender_12_out = {{31{decoder_1_out13}}, decoder_1_out13};  // Bit_Extender bit_extender_12
  assign bit_extender_13_out = {{31{decoder_1_out3}}, decoder_1_out3};  // Bit_Extender bit_extender_13
  assign bit_extender_14_out = {{31{decoder_1_out15}}, decoder_1_out15};  // Bit_Extender bit_extender_14
  AND32 and32_1 (.A(bit_extender_1_out), .B(A), .Result(and32_1_result));
  AND32 and32_2 (.A(bit_extender_1_out), .B(B), .Result(and32_2_result));
  AND32 and32_3 (.A(bit_extender_2_out), .B(A), .Result(and32_3_result));
  AND32 and32_4 (.A(bit_extender_2_out), .B(B), .Result(and32_4_result));
  AND32 and32_5 (.A(bit_extender_3_out), .B(A), .Result(and32_5_result));
  AND32 and32_6 (.A(bit_extender_3_out), .B(B), .Result(and32_6_result));
  AND32 and32_7 (.A(bit_extender_4_out), .B(A), .Result(and32_7_result));
  AND32 and32_8 (.A(bit_extender_4_out), .B(B), .Result(and32_8_result));
  AND32 and32_9 (.A(bit_extender_5_out), .B(A), .Result(and32_9_result));
  AND32 and32_10 (.A(bit_extender_5_out), .B(B), .Result(and32_10_result));
  AND32 and32_11 (.A(bit_extender_6_out), .B(A), .Result(and32_11_result));
  AND32 and32_12 (.A(bit_extender_6_out), .B(B), .Result(and32_12_result));
  AND32 and32_13 (.A(bit_extender_7_out), .B(A), .Result(and32_13_result));
  AND32 and32_14 (.A(bit_extender_7_out), .B(B), .Result(and32_14_result));
  AND32 and32_15 (.A(bit_extender_8_out), .B(A), .Result(and32_15_result));
  AND32 and32_16 (.A(bit_extender_8_out), .B(B), .Result(and32_16_result));
  AND32 and32_17 (.A(bit_extender_9_out), .B(A), .Result(and32_17_result));
  AND32 and32_18 (.A(bit_extender_9_out), .B(B), .Result(and32_18_result));
  AND32 and32_19 (.A(bit_extender_10_out), .B(A), .Result(and32_19_result));
  AND32 and32_20 (.A(bit_extender_10_out), .B(B), .Result(and32_20_result));
  AND32 and32_21 (.A(bit_extender_11_out), .B(A), .Result(and32_21_result));
  AND32 and32_22 (.A(bit_extender_11_out), .B(B), .Result(and32_22_result));
  AND32 and32_23 (.A(bit_extender_12_out), .B(A), .Result(and32_23_result));
  AND32 and32_24 (.A(bit_extender_12_out), .B(B), .Result(and32_24_result));
  AND32 and32_25 (.A(bit_extender_13_out), .B(A), .Result(and32_25_result));
  AND32 and32_26 (.A(bit_extender_13_out), .B(B), .Result(and32_26_result));
  AND32 and32_27 (.A(bit_extender_14_out), .B(B), .Result(and32_27_result));
  Adder32 adder32_1 (.A(and32_1_result), .B(and32_2_result), .OverFlow(OverFlow), .Result(adder32_1_result));
  Shifter_Left shifter_left_1 (.A(and32_3_result), .B(and32_4_result), .Result(shifter_left_1_result));
  compare compare_1 (.A(and32_5_result), .B(and32_6_result), .Result(compare_1_result));
  XOR32 xor32_1 (.A(and32_7_result), .B(and32_8_result), .Result(xor32_1_result));
  Shifter_Right shifter_right_1 (.A(and32_9_result), .B(and32_10_result), .Result(shifter_right_1_result));
  OR32 or32_1 (.A(and32_11_result), .B(and32_12_result), .Result(or32_1_result));
  AND32 and32_28 (.A(and32_13_result), .B(and32_14_result), .Result(and32_28_result));
  Mult mult_1 (.A(and32_15_result), .B(and32_16_result), .Result(mult_1_result));
  mulh mulh_1 (.A(and32_17_result), .B(and32_18_result), .Result(mulh_1_result));
  Mulhu mulhu_1 (.A(and32_19_result), .B(and32_20_result), .Result(mulhu_1_result));
  subtract subtract_1 (.A(and32_21_result), .B(and32_22_result), .Result(subtract_1_result));
  signed_sra signed_sra_1 (.A(and32_23_result), .B(and32_24_result), .Result(signed_sra_1_result));
  compareu compareu_1 (.A(and32_25_result), .B(and32_26_result), .Result(compareu_1_result));
  OR32 or32_2 (.A(adder32_1_result), .B(shifter_left_1_result), .Result(or32_2_result));
  OR32 or32_3 (.A(compare_1_result), .B(xor32_1_result), .Result(or32_3_result));
  OR32 or32_4 (.A(shifter_right_1_result), .B(or32_1_result), .Result(or32_4_result));
  OR32 or32_5 (.A(and32_28_result), .B(mult_1_result), .Result(or32_5_result));
  OR32 or32_6 (.A(mulh_1_result), .B(mulhu_1_result), .Result(or32_6_result));
  OR32 or32_7 (.A(subtract_1_result), .B(signed_sra_1_result), .Result(or32_7_result));
  OR32 or32_8 (.A(compareu_1_result), .B(and32_27_result), .Result(or32_8_result));
  OR32 or32_9 (.A(or32_2_result), .B(or32_3_result), .Result(or32_9_result));
  OR32 or32_10 (.A(or32_4_result), .B(or32_5_result), .Result(or32_10_result));
  OR32 or32_11 (.A(or32_6_result), .B(or32_7_result), .Result(or32_11_result));
  OR32 or32_12 (.A(or32_9_result), .B(or32_10_result), .Result(or32_12_result));
  OR32 or32_13 (.A(or32_12_result), .B(or32_14_result), .Result(Result));
  OR32 or32_14 (.A(or32_11_result), .B(or32_8_result), .Result(or32_14_result));
  Comparator #(.mode("unsigned"), .width(32)) comparator_1 (
    .a({32{1'b0}}), .b(Result), .eq(comparator_1_eq));  // open: gt, lt
  Multiplexer #(.enable("true")) multiplexer_1 (.in0(1'b0), .in1(1'b1), .out(Zero), .sel(comparator_1_eq));  // open: en
endmodule

// decoder
module decode (
  input  [31:0] in_1,
  output [6:0] func7,
  output [4:0] rd,
  output [2:0] func3,
  output [4:0] rs1,
  output [4:0] rs2,
  output r,
  output i,
  output beq,
  output sw,
  output [31:0] imm,
  output lw
);

  wire comparator_2_eq, l_out, sbtype_out, stype_out, test;
  wire [2:0] and_3_out_2, and_4_out_2, and_5_out, and_6_out, and_7_out_2;
  wire [4:0] and_3_out, and_3_out_3, and_3_out_4, and_4_out, and_4_out_3, and_5_out_2, and_5_out_3,
       and_5_out_4, and_6_out_2, and_6_out_3, and_6_out_4, and_7_out, and_7_out_3;
  wire [6:0] and_5_out_5, and_6_out_5;
  wire [11:0] and_4_out_4, and_7_out_4;
  wire [24:0] bit_extender_1_out, bit_extender_2_out, bit_extender_3_out, bit_extender_4_out,
       bit_extender_5_out;
  wire [31:0] bit_extender_6_out, bit_extender_7_out, bit_extender_8_out, bit_extender_9_out;

  Comparator #(.width(3)) comparator_1 (.a(3'b010), .b(func3), .eq(test));  // open: gt, lt
  and rtype (r, in_1[0], in_1[1], ~in_1[2], ~in_1[3], in_1[4], in_1[5], ~in_1[6]);  // AND_Gate
  and itype (i, in_1[0], in_1[1], ~in_1[2], ~in_1[3], in_1[4], ~in_1[5], ~in_1[6]);  // AND_Gate
  and stype (stype_out, in_1[0], in_1[1], ~in_1[2], ~in_1[3], ~in_1[4], in_1[5], ~in_1[6]);  // AND_Gate
  and sbtype (sbtype_out, in_1[0], in_1[1], ~in_1[2], ~in_1[3], ~in_1[4], in_1[5], in_1[6]);  // AND_Gate
  and l (l_out, in_1[0], in_1[1], ~in_1[2], ~in_1[3], ~in_1[4], ~in_1[5], ~in_1[6]);  // AND_Gate
  assign bit_extender_1_out = {{24{r}}, r};  // Bit_Extender bit_extender_1
  assign bit_extender_2_out = {{24{i}}, i};  // Bit_Extender bit_extender_2
  assign bit_extender_3_out = {{24{stype_out}}, stype_out};  // Bit_Extender bit_extender_3
  assign bit_extender_4_out = {{24{sbtype_out}}, sbtype_out};  // Bit_Extender bit_extender_4
  assign bit_extender_5_out = {{24{l_out}}, l_out};  // Bit_Extender bit_extender_5
  and and_1 (sw, stype_out, test);
  and and_2 (lw, test, l_out);
  assign {func7, and_3_out_4, and_3_out_3, and_3_out_2, and_3_out} = bit_extender_1_out & in_1[31:7];  // AND_Gate and_3, 25 bits wide
  assign {and_4_out_4, and_4_out_3, and_4_out_2, and_4_out} = bit_extender_2_out & in_1[31:7];  // AND_Gate and_4, 25 bits wide
  assign {and_5_out_5, and_5_out_3, and_5_out_2, and_5_out, and_5_out_4} = bit_extender_3_out & in_1[31:7];  // AND_Gate and_5, 25 bits wide
  assign {and_6_out_5, and_6_out_3, and_6_out_2, and_6_out, and_6_out_4} = bit_extender_4_out & in_1[31:7];  // AND_Gate and_6, 25 bits wide
  assign {and_7_out_4, and_7_out_3, and_7_out_2, and_7_out} = bit_extender_5_out & in_1[31:7];  // AND_Gate and_7, 25 bits wide
  Comparator #(.width(3)) comparator_2 (.a(3'b000), .b(func3), .eq(comparator_2_eq));  // open: gt, lt
  and and_8 (beq, comparator_2_eq, sbtype_out);
  assign bit_extender_6_out = {{20{and_4_out_4[11]}}, and_4_out_4};  // Bit_Extender bit_extender_6
  assign bit_extender_7_out = {{20{and_5_out_5[6]}}, {and_5_out_5, and_5_out_4}};  // Bit_Extender bit_extender_7
  assign bit_extender_8_out = {{19{and_6_out_5[6]}}, {and_6_out_5[6], and_6_out_4[0], and_6_out_5[5:0], and_6_out_4[4:1], 1'b0}};  // Bit_Extender bit_extender_8
  assign bit_extender_9_out = {{20{and_7_out_4[11]}}, and_7_out_4};  // Bit_Extender bit_extender_9
  assign rd = and_3_out | and_4_out | and_7_out;  // OR_Gate or_1, 5 bits wide
  assign func3 = and_3_out_2 | and_4_out_2 | and_5_out | and_6_out | and_7_out_2;  // OR_Gate or_2, 3 bits wide
  assign rs1 = and_3_out_3 | and_4_out_3 | and_5_out_2 | and_6_out_2 | and_7_out_3;  // OR_Gate or_3, 5 bits wide
  assign rs2 = and_3_out_4 | and_5_out_3 | and_6_out_3;  // OR_Gate or_4, 5 bits wide
  assign imm = bit_extender_6_out | bit_extender_7_out | bit_extender_8_out | bit_extender_9_out;  // OR_Gate or_5, 32 bits wide

  // Other names for the same wires on the sheet: f3[2:0] = func3
endmodule

// reg
module regfile (
  input  [4:0] rd,
  input  reset,
  input  clk,
  input  [4:0] rs1,
  input  rw_en,
  input  [4:0] rs2,
  input  [31:0] wd,
  output [31:0] rd1,
  output [31:0] rd2
);

  wire decoder_1_out1, decoder_1_out2, decoder_1_out5, decoder_1_out6, decoder_1_out7, decoder_1_out8,
       decoder_1_out9, decoder_1_out10;
  wire [31:0] a0_q, ra_q, s0_q, s1_q, sp_q, t0_q, t1_q, t2_q;

  Decoder #(.select(5)) decoder_1 (
    .out1(decoder_1_out1), .out2(decoder_1_out2), .out5(decoder_1_out5), .out6(decoder_1_out6),
    .out7(decoder_1_out7), .out8(decoder_1_out8), .out9(decoder_1_out9), .out10(decoder_1_out10), .sel(rd),
    .en(rw_en));  // open: out0, out3, out4, out11, out12, out13, out14, out15, out16, out17, out18, out19, out20, out21, out22, out23, out24, out25, out26, out27, out28, out29, out30, out31
  Register #(.width(32)) ra (.D(wd), .en(decoder_1_out1), .Q(ra_q), .clk(clk), .clr(reset));
  Register #(.width(32)) sp (.D(wd), .en(decoder_1_out2), .Q(sp_q), .clk(clk), .clr(reset));
  Register #(.width(32)) t0 (.D(wd), .en(decoder_1_out5), .Q(t0_q), .clk(clk), .clr(reset));
  Register #(.width(32)) t1 (.D(wd), .en(decoder_1_out6), .Q(t1_q), .clk(clk), .clr(reset));
  Register #(.width(32)) t2 (.D(wd), .en(decoder_1_out7), .Q(t2_q), .clk(clk), .clr(reset));
  Register #(.width(32)) s0 (.D(wd), .en(decoder_1_out8), .Q(s0_q), .clk(clk), .clr(reset));
  Register #(.width(32)) s1 (.D(wd), .en(decoder_1_out9), .Q(s1_q), .clk(clk), .clr(reset));
  Register #(.width(32)) a0 (.D(wd), .en(decoder_1_out10), .Q(a0_q), .clk(clk), .clr(reset));
  Multiplexer #(.enable("true"), .select(5), .width(32)) multiplexer_1 (
    .in0({32{1'b0}}), .in1(ra_q), .in2(sp_q), .in5(t0_q), .in6(t1_q), .in7(t2_q), .in8(s0_q), .in9(s1_q),
    .in10(a0_q), .out(rd1), .sel(rs1));  // open: in3, in4, in11, in12, in13, in14, in15, in16, in17, in18, in19, in20, in21, in22, in23, in24, in25, in26, in27, in28, in29, in30, in31, en
  Multiplexer #(.enable("true"), .select(5), .width(32)) multiplexer_2 (
    .in0({32{1'b0}}), .in1(ra_q), .in2(sp_q), .in5(t0_q), .in6(t1_q), .in7(t2_q), .in8(s0_q), .in9(s1_q),
    .in10(a0_q), .out(rd2), .sel(rs2));  // open: in3, in4, in11, in12, in13, in14, in15, in16, in17, in18, in19, in20, in21, in22, in23, in24, in25, in26, in27, in28, in29, in30, in31, en
endmodule

// op
module opcodes (
  input  [6:0] func7,
  input  [2:0] func3,
  input  r,
  input  i,
  output [3:0] op
);

  wire en, nzero, zero;
  wire [3:0] multiplexer_1_out, multiplexer_2_out, multiplexer_3_out, multiplexer_4_out, multiplexer_5_out,
       multiplexer_6_out, multiplexer_7_out, multiplexer_8_out, multiplexer_9_out;

  Comparator #(.width(7)) comparator_1 (.a(func7), .b(7'b0100000), .eq(nzero));  // open: gt, lt
  or or_1 (en, r, i);
  Comparator #(.width(7)) comparator_2 (.a(func7), .b({7{1'b0}}), .eq(zero));  // open: gt, lt
  Multiplexer #(.enable("true"), .width(4)) multiplexer_1 (
    .in0(4'b1110), .in1(4'b1100), .out(multiplexer_1_out), .sel(nzero), .en(r));
  Multiplexer #(.enable("true"), .width(4)) multiplexer_2 (
    .in0(multiplexer_1_out), .in1(4'b0000), .out(multiplexer_2_out), .sel(zero), .en(en));
  Multiplexer #(.enable("true"), .width(4)) multiplexer_3 (
    .in0(4'b1110), .in1(4'b0001), .out(multiplexer_3_out), .sel(zero), .en(en));
  Multiplexer #(.enable("true"), .width(4)) multiplexer_4 (
    .in0(4'b1110), .in1(4'b0010), .out(multiplexer_4_out), .sel(zero), .en(en));
  Multiplexer #(.enable("true"), .width(4)) multiplexer_5 (
    .in0(4'b1110), .in1(4'b0011), .out(multiplexer_5_out), .sel(zero), .en(en));
  Multiplexer #(.enable("true"), .width(4)) multiplexer_6 (
    .in0(4'b1110), .in1(4'b0100), .out(multiplexer_6_out), .sel(zero), .en(en));
  Multiplexer #(.enable("true"), .width(4)) multiplexer_7 (
    .in0(4'b1110), .in1(4'b0101), .out(multiplexer_7_out), .sel(zero), .en(en));
  Multiplexer #(.enable("true"), .width(4)) multiplexer_8 (
    .in0(4'b1110), .in1(4'b0110), .out(multiplexer_8_out), .sel(zero), .en(en));
  Multiplexer #(.enable("true"), .width(4)) multiplexer_9 (
    .in0(4'b1110), .in1(4'b0111), .out(multiplexer_9_out), .sel(zero), .en(en));
  Multiplexer #(.select(3), .width(4)) multiplexer_10 (
    .in0(multiplexer_2_out), .in1(multiplexer_3_out), .in2(multiplexer_4_out), .in3(multiplexer_5_out),
    .in4(multiplexer_6_out), .in5(multiplexer_7_out), .in6(multiplexer_8_out), .in7(multiplexer_9_out),
    .out(op));  // open: sel

  // Other names for the same wires on the sheet: f3[2:0] = func3; subt = r
endmodule

module processor (
  input  in_1,
  output [2:0] out_2,
  output [31:0] out_3
);

  wire and_1_out, b, clk, i, l, or_1_out, r, s, write, zero;
  wire [3:0] aluop, multiplexer_3_out;
  wire [4:0] rd, rs1, rs2;
  wire [6:0] f7;
  wire [31:0] adder32_1_result, adder32_2_result, datamem_dout, imm, instr, multiplexer_1_out,
       multiplexer_2_out, multiplexer_4_out, pc_q, rd2, regfile_1_rd1;

  Register #(.width(32)) pc (.D(multiplexer_1_out), .clk(clk), .Q(pc_q), .clr(in_1));  // open: en
  regfile regfile_1 (
    .rw_en(write), .rd(rd), .wd(multiplexer_4_out), .reset(in_1), .clk(clk), .rs2(rs2), .rs1(rs1), .rd2(rd2),
    .rd1(regfile_1_rd1));
  Adder32 adder32_1 (.A(pc_q), .B(32'h4), .Result(adder32_1_result));  // open: OverFlow
  Adder32 adder32_2 (.A(pc_q), .B(imm), .Result(adder32_2_result));  // open: OverFlow
  and and_1 (and_1_out, b, zero);
  // ROM #(.addrWidth(24), .line("quad")) Imem: pin names not known; wires that end beside it: pc_q[23:0], instr[31:24], instr[23:16], instr[15:8], instr[7:0]
  Multiplexer #(.width(32)) multiplexer_1 (
    .in0(adder32_1_result), .in1(adder32_2_result), .out(multiplexer_1_out), .sel(and_1_out));
  Multiplexer #(.width(32)) multiplexer_2 (.in0(imm), .in1(rd2), .out(multiplexer_2_out), .sel(or_1_out));
  or or_1 (or_1_out, b, r);
  alucirc alucirc_1 (
    .ALUSel(multiplexer_3_out), .A(regfile_1_rd1), .B(multiplexer_2_out), .Result(out_3), .Zero(zero));  // open: OverFlow
  Multiplexer #(.width(4)) multiplexer_3 (.in0(aluop), .in1(4'b1100), .out(multiplexer_3_out), .sel(b));
  Clock clock_1 (.out(clk));
  decode decode_1 (
    .in_1(instr), .func7(f7), .rd(rd), .func3(out_2), .rs1(rs1), .rs2(rs2), .imm(imm), .i(i), .r(r), .sw(s),
    .lw(l), .beq(b));
  RAM #(.addrWidth(24), .dataWidth(32)) datamem (
    .addr(out_3[23:0]), .we(s), .oe(l), .clk(clk), .din(rd2), .dout(datamem_dout));
  opcodes opcodes_1 (.func7(f7), .r(r), .i(i), .func3(out_2), .op(aluop));
  or or_2 (write, i, r, l);
  Multiplexer #(.width(32)) multiplexer_4 (.in0(out_3), .in1(datamem_dout), .out(multiplexer_4_out), .sel(l));

  // Other names for the same wires on the sheet: f3[2:0] = out_2; Res[31:0] = out_3; reset = in_1

  // Notes on the sheet:
  //   contents of Imem (hex, n*v repeats v):
  //   5*0 50 2 93 0 53 3 33 40 62 82 b3 0 13 13 93 0 73 23 b3 0 73 13 33 0 73 33 b3 0 d3 a4 13 0 74 54 b3
  //   0 94 45 33 0 60 28 23 1 0 22 83 8 94 0 63
  //   System Controls
endmodule
