// Logisim project register.circ as structural Verilog: 2 circuits, main circuit regfile
module regfile (
  input  [4:0] rd,
  input  rw_en,
  input  clk,
  input  [4:0] rs1,
  input  [4:0] rs2,
  input  [31:0] wd,
  output [31:0] rd1,
  output [31:0] rd2
);

  wire decoder_1_out1, decoder_1_out2, decoder_1_out5, decoder_1_out6, decoder_1_out7, decoder_1_out8,
       decoder_1_out9, decoder_1_out10;
  wire [31:0] a0_q, ra_q, s0_q, s1_q, sp_q, t0_q, t1_q, t2_q;

  Decoder #(.select(5), .disabled(0)) decoder_1 (
    .out1(decoder_1_out1), .out2(decoder_1_out2), .out5(decoder_1_out5), .out6(decoder_1_out6),
    .out7(decoder_1_out7), .out8(decoder_1_out8), .out9(decoder_1_out9), .out10(decoder_1_out10), .sel(rd),
    .en(rw_en));  // open: out0, out3, out4, out11, out12, out13, out14, out15, out16, out17, out18, out19, out20, out21, out22, out23, out24, out25, out26, out27, out28, out29, out30, out31
  Register #(.width(32)) ra (.D(wd), .en(decoder_1_out1), .Q(ra_q), .clk(clk));  // open: clr
  Register #(.width(32)) sp (.D(wd), .en(decoder_1_out2), .Q(sp_q), .clk(clk));  // open: clr
  Register #(.width(32)) t0 (.D(wd), .en(decoder_1_out5), .Q(t0_q), .clk(clk));  // open: clr
  Register #(.width(32)) t1 (.D(wd), .en(decoder_1_out6), .Q(t1_q), .clk(clk));  // open: clr
  Register #(.width(32)) t2 (.D(wd), .en(decoder_1_out7), .Q(t2_q), .clk(clk));  // open: clr
  Register #(.width(32)) s0 (.D(wd), .en(decoder_1_out8), .Q(s0_q), .clk(clk));  // open: clr
  Register #(.width(32)) s1 (.D(wd), .en(decoder_1_out9), .Q(s1_q), .clk(clk));  // open: clr
  Register #(.width(32)) a0 (.D(wd), .en(decoder_1_out10), .Q(a0_q), .clk(clk));  // open: clr
  Multiplexer #(.select(5), .width(32), .enable("false")) multiplexer_1 (
    .in0({32{1'b0}}), .in1(ra_q), .in2(sp_q), .in5(t0_q), .in6(t1_q), .in7(t2_q), .in8(s0_q), .in9(s1_q),
    .in10(a0_q), .out(rd1), .sel(rs1));  // open: in3, in4, in11, in12, in13, in14, in15, in16, in17, in18, in19, in20, in21, in22, in23, in24, in25, in26, in27, in28, in29, in30, in31
  Multiplexer #(.select(5), .width(32), .enable("false")) multiplexer_2 (
    .in0({32{1'b0}}), .in1(ra_q), .in2(sp_q), .in5(t0_q), .in6(t1_q), .in7(t2_q), .in8(s0_q), .in9(s1_q),
    .in10(a0_q), .out(rd2), .sel(rs2));  // open: in3, in4, in11, in12, in13, in14, in15, in16, in17, in18, in19, in20, in21, in22, in23, in24, in25, in26, in27, in28, in29, in30, in31
endmodule

module main (
  input  RegWEn,
  input  [4:0] rs2,
  input  [4:0] rs1,
  input  [4:0] rd,
  input  [31:0] wd,
  output [31:0] rd1,
  output [31:0] rd2
);

  wire Clock_out;

  Clock Clock (.out(Clock_out));
  regfile regfile_1 (.rw_en(RegWEn), .wd(wd), .rs1(rs1), .rd1(rd1), .rs2(rs2), .rd2(rd2), .rd(rd), .clk(Clock_out));
endmodule
